// Logisim project CPU .circ as structural Verilog: 41 circuits, main circuit main
module main (
);

  wire CLK, END, RAM_E, RAM_S, RESET, twoscomp_to_bcd_1_sign, twoscomp_to_bcd_2_sign, twoscomp_to_bcd_3_sign,
       twoscomp_to_bcd_4_sign;
  wire [3:0] bin_to_bcd_r_1_hundreds, bin_to_bcd_r_1_tens, bin_to_bcd_r_1_units, bin_to_bcd_r_2_hundreds,
       bin_to_bcd_r_2_tens, bin_to_bcd_r_2_units, bin_to_bcd_r_3_hundreds, bin_to_bcd_r_3_tens,
       bin_to_bcd_r_3_units, bin_to_bcd_r_4_hundreds, bin_to_bcd_r_4_tens, bin_to_bcd_r_4_units,
       twoscomp_to_bcd_1_hundreds, twoscomp_to_bcd_1_tens, twoscomp_to_bcd_1_units,
       twoscomp_to_bcd_2_hundreds, twoscomp_to_bcd_2_tens, twoscomp_to_bcd_2_units,
       twoscomp_to_bcd_3_hundreds, twoscomp_to_bcd_3_tens, twoscomp_to_bcd_3_units,
       twoscomp_to_bcd_4_hundreds, twoscomp_to_bcd_4_tens, twoscomp_to_bcd_4_units;
  wire [7:0] ACC, BUS, IAR, IR, R0, R1, R2, R3, RAM_ADD, RAM_IN, RAM_OUT;

  Button button_1 (.out(RESET));
  LED led_1 (.in(END));
  Clock u_CLK (.out(CLK));
  Hex_Digit_Display hex_digit_display_1 (.value(R0[3:0]));  // open: dp
  Hex_Digit_Display hex_digit_display_2 (.value(R0[7:4]));  // open: dp
  Hex_Digit_Display hex_digit_display_3 (.value(R2[3:0]));  // open: dp
  Hex_Digit_Display hex_digit_display_4 (.value(R2[7:4]));  // open: dp
  Hex_Digit_Display hex_digit_display_5 (.value(bin_to_bcd_r_1_hundreds));  // open: dp
  Hex_Digit_Display hex_digit_display_6 (.value(bin_to_bcd_r_1_tens));  // open: dp
  Hex_Digit_Display hex_digit_display_7 (.value(bin_to_bcd_r_2_hundreds));  // open: dp
  Hex_Digit_Display hex_digit_display_8 (.value(bin_to_bcd_r_2_tens));  // open: dp
  RAM #(.bus("separate")) ram_1 (
    .addr(RAM_ADD), .din(RAM_IN), .data(RAM_OUT), .str(RAM_S), .clk(RAM_S), .ld(RAM_E), .clr(RESET));  // open: sel
  _7_Segment_Display u_7_segment_display_1 (.g(twoscomp_to_bcd_1_sign));  // open: f, a, b, e, d, c, dp
  Hex_Digit_Display hex_digit_display_9 (.value(bin_to_bcd_r_1_units));  // open: dp
  BIN_TO_BCD_R bin_to_bcd_r_1 (
    .binary(R0), .units(bin_to_bcd_r_1_units), .tens(bin_to_bcd_r_1_tens), .hundreds(bin_to_bcd_r_1_hundreds));
  _7_Segment_Display u_7_segment_display_2 (.g(twoscomp_to_bcd_2_sign));  // open: f, a, b, e, d, c, dp
  Hex_Digit_Display hex_digit_display_10 (.value(bin_to_bcd_r_2_units));  // open: dp
  BIN_TO_BCD_R bin_to_bcd_r_2 (
    .binary(R2), .units(bin_to_bcd_r_2_units), .tens(bin_to_bcd_r_2_tens), .hundreds(bin_to_bcd_r_2_hundreds));
  Hex_Digit_Display hex_digit_display_11 (.value(twoscomp_to_bcd_1_tens));  // open: dp
  Hex_Digit_Display hex_digit_display_12 (.value(twoscomp_to_bcd_1_hundreds));  // open: dp
  Hex_Digit_Display hex_digit_display_13 (.value(twoscomp_to_bcd_2_hundreds));  // open: dp
  Hex_Digit_Display hex_digit_display_14 (.value(twoscomp_to_bcd_2_tens));  // open: dp
  Hex_Digit_Display hex_digit_display_15 (.value(twoscomp_to_bcd_1_units));  // open: dp
  TWOSCOMP_TO_BCD twoscomp_to_bcd_1 (
    .binary(R0), .units(twoscomp_to_bcd_1_units), .tens(twoscomp_to_bcd_1_tens),
    .hundreds(twoscomp_to_bcd_1_hundreds), .sign(twoscomp_to_bcd_1_sign));
  Hex_Digit_Display hex_digit_display_16 (.value(twoscomp_to_bcd_2_units));  // open: dp
  TWOSCOMP_TO_BCD twoscomp_to_bcd_2 (
    .binary(R2), .units(twoscomp_to_bcd_2_units), .tens(twoscomp_to_bcd_2_tens),
    .hundreds(twoscomp_to_bcd_2_hundreds), .sign(twoscomp_to_bcd_2_sign));
  Hex_Digit_Display hex_digit_display_17 (.value(R1[7:4]));  // open: dp
  Hex_Digit_Display hex_digit_display_18 (.value(R3[7:4]));  // open: dp
  Hex_Digit_Display hex_digit_display_19 (.value(bin_to_bcd_r_3_hundreds));  // open: dp
  Hex_Digit_Display hex_digit_display_20 (.value(R1[3:0]));  // open: dp
  Hex_Digit_Display hex_digit_display_21 (.value(R3[3:0]));  // open: dp
  Hex_Digit_Display hex_digit_display_22 (.value(bin_to_bcd_r_4_hundreds));  // open: dp
  Hex_Digit_Display hex_digit_display_23 (.value(bin_to_bcd_r_3_units));  // open: dp
  Hex_Digit_Display hex_digit_display_24 (.value(bin_to_bcd_r_3_tens));  // open: dp
  BIN_TO_BCD_R bin_to_bcd_r_3 (
    .binary(R1), .units(bin_to_bcd_r_3_units), .tens(bin_to_bcd_r_3_tens), .hundreds(bin_to_bcd_r_3_hundreds));
  Hex_Digit_Display hex_digit_display_25 (.value(bin_to_bcd_r_4_tens));  // open: dp
  Hex_Digit_Display hex_digit_display_26 (.value(bin_to_bcd_r_4_units));  // open: dp
  BIN_TO_BCD_R bin_to_bcd_r_4 (
    .binary(R3), .units(bin_to_bcd_r_4_units), .tens(bin_to_bcd_r_4_tens), .hundreds(bin_to_bcd_r_4_hundreds));
  CPU cpu_1 (
    .R0(R0), .R1(R1), .R2(R2), .R3(R3), .BUS(BUS), .ACC(ACC), .IAR(IAR), .RAM_Address(RAM_ADD),
    .RAM_ENABLE(RAM_E), .RAM_SET(RAM_S), .END(END), .IR(IR), .RAM_Data_In(RAM_IN), .RAM_Data_Out(RAM_OUT),
    .in_3(RESET), .CLK(CLK));
  _7_Segment_Display u_7_segment_display_3 (.g(twoscomp_to_bcd_3_sign));  // open: f, a, b, e, d, c, dp
  Hex_Digit_Display hex_digit_display_27 (.value(twoscomp_to_bcd_3_hundreds));  // open: dp
  _7_Segment_Display u_7_segment_display_4 (.g(twoscomp_to_bcd_4_sign));  // open: f, a, b, e, d, c, dp
  Hex_Digit_Display hex_digit_display_28 (.value(twoscomp_to_bcd_4_hundreds));  // open: dp
  Hex_Digit_Display hex_digit_display_29 (.value(twoscomp_to_bcd_3_units));  // open: dp
  Hex_Digit_Display hex_digit_display_30 (.value(twoscomp_to_bcd_3_tens));  // open: dp
  TWOSCOMP_TO_BCD twoscomp_to_bcd_3 (
    .binary(R1), .units(twoscomp_to_bcd_3_units), .tens(twoscomp_to_bcd_3_tens),
    .hundreds(twoscomp_to_bcd_3_hundreds), .sign(twoscomp_to_bcd_3_sign));
  Hex_Digit_Display hex_digit_display_31 (.value(twoscomp_to_bcd_4_tens));  // open: dp
  Hex_Digit_Display hex_digit_display_32 (.value(twoscomp_to_bcd_4_units));  // open: dp
  TWOSCOMP_TO_BCD twoscomp_to_bcd_4 (
    .binary(R3), .units(twoscomp_to_bcd_4_units), .tens(twoscomp_to_bcd_4_tens),
    .hundreds(twoscomp_to_bcd_4_hundreds), .sign(twoscomp_to_bcd_4_sign));
  Hex_Digit_Display hex_digit_display_33 (.value(BUS[7:4]));  // open: dp
  Hex_Digit_Display hex_digit_display_34 (.value(ACC[7:4]));  // open: dp
  Hex_Digit_Display hex_digit_display_35 (.value(IAR[7:4]));  // open: dp
  Hex_Digit_Display hex_digit_display_36 (.value(IR[7:4]));  // open: dp
  Hex_Digit_Display hex_digit_display_37 (.value(BUS[3:0]));  // open: dp
  Hex_Digit_Display hex_digit_display_38 (.value(ACC[3:0]));  // open: dp
  Hex_Digit_Display hex_digit_display_39 (.value(IAR[3:0]));  // open: dp
  Hex_Digit_Display hex_digit_display_40 (.value(IR[3:0]));  // open: dp

  // Notes on the sheet:
  //   R0
  //   R2
  //   HEX
  //   HEX
  //   UNSIGNED
  //   UNSIGNED
  //   SIGNED
  //   SIGNED
  //   HEX
  //   R1
  //   HEX
  //   R3
  //   UNSIGNED
  //   UNSIGNED
  //   SIGNED
  //   SIGNED
  //   BUS
  //   ACC
  //   IAR
  //   IR
  //   HEX
  //   HEX
  //   HEX
  //   HEX
endmodule

module MEM_1_BIT (
  input  D,
  input  E,
  output out_3
);

  wire nand_1_out, nand_2_out, nand_4_out;

  nand nand_1 (nand_1_out, D, E);
  nand nand_2 (nand_2_out, nand_1_out, E);
  nand nand_3 (out_3, nand_1_out, nand_4_out);
  nand nand_4 (nand_4_out, out_3, nand_2_out);
endmodule

module MEM_1_BYTE (
  input  [7:0] in_1,
  input  in_2,
  output [7:0] out_3
);

  MEM_1_BIT mem_1_bit_1 (.D(in_1[0]), .E(in_2), .out_3(out_3[0]));
  MEM_1_BIT mem_1_bit_2 (.D(in_1[1]), .E(in_2), .out_3(out_3[1]));
  MEM_1_BIT mem_1_bit_3 (.D(in_1[2]), .E(in_2), .out_3(out_3[2]));
  MEM_1_BIT mem_1_bit_4 (.D(in_1[3]), .E(in_2), .out_3(out_3[3]));
  MEM_1_BIT mem_1_bit_5 (.D(in_1[4]), .E(in_2), .out_3(out_3[4]));
  MEM_1_BIT mem_1_bit_6 (.D(in_1[5]), .E(in_2), .out_3(out_3[5]));
  MEM_1_BIT mem_1_bit_7 (.D(in_1[6]), .E(in_2), .out_3(out_3[6]));
  MEM_1_BIT mem_1_bit_8 (.D(in_1[7]), .E(in_2), .out_3(out_3[7]));
endmodule

module ENABLE (
  input  [7:0] in_1,
  input  in_2,
  output [7:0] out_3
);

  wire and_1_out, and_2_out, and_3_out, and_4_out, and_5_out, and_6_out, and_7_out, and_8_out;

  and and_1 (and_1_out, in_1[0], in_2);
  and and_2 (and_2_out, in_1[1], in_2);
  and and_3 (and_3_out, in_1[2], in_2);
  and and_4 (and_4_out, in_1[3], in_2);
  and and_5 (and_5_out, in_1[4], in_2);
  and and_6 (and_6_out, in_1[5], in_2);
  and and_7 (and_7_out, in_1[6], in_2);
  and and_8 (and_8_out, in_1[7], in_2);
  assign out_3[0] = in_2 ? and_1_out : 1'bz;  // Controlled_Buffer controlled_buffer_1
  assign out_3[1] = in_2 ? and_2_out : 1'bz;  // Controlled_Buffer controlled_buffer_2
  assign out_3[2] = in_2 ? and_3_out : 1'bz;  // Controlled_Buffer controlled_buffer_3
  assign out_3[3] = in_2 ? and_4_out : 1'bz;  // Controlled_Buffer controlled_buffer_4
  assign out_3[4] = in_2 ? and_5_out : 1'bz;  // Controlled_Buffer controlled_buffer_5
  assign out_3[5] = in_2 ? and_6_out : 1'bz;  // Controlled_Buffer controlled_buffer_6
  assign out_3[6] = in_2 ? and_7_out : 1'bz;  // Controlled_Buffer controlled_buffer_7
  assign out_3[7] = in_2 ? and_8_out : 1'bz;  // Controlled_Buffer controlled_buffer_8
endmodule

module REGISTER_8 (
  input  [7:0] in_1,
  input  in_2,
  input  in_3,
  output [7:0] out_4,
  output [7:0] out_5
);

  wire [7:0] enable_1_out_3;

  MEM_1_BYTE mem_1_byte_1 (.in_1(in_1), .out_3(out_4), .in_2(in_2));
  ENABLE enable_1 (.in_1(out_4), .out_3(enable_1_out_3), .in_2(in_3));
  assign out_5 = in_3 ? enable_1_out_3 : 8'bz;  // Controlled_Buffer controlled_buffer_1
endmodule

module DECODER_4x16 (
  input  [3:0] in_1,
  output L,
  output out_3,
  output out_4,
  output out_5,
  output out_6,
  output out_7,
  output out_8,
  output out_9,
  output out_10,
  output out_11,
  output out_12,
  output out_13,
  output out_14,
  output out_15,
  output out_16,
  output M
);

  wire not_1_out, not_2_out, not_3_out, not_4_out;

  not not_1 (not_1_out, in_1[0]);
  not not_2 (not_2_out, in_1[1]);
  not not_3 (not_3_out, in_1[2]);
  not not_4 (not_4_out, in_1[3]);
  and and_1 (L, not_4_out, not_3_out, not_2_out, not_1_out);
  and and_2 (out_3, not_4_out, not_3_out, not_2_out, in_1[0]);
  and and_3 (out_4, not_4_out, not_3_out, in_1[1], not_1_out);
  and and_4 (out_5, not_4_out, not_3_out, in_1[1], in_1[0]);
  and and_5 (out_6, not_4_out, in_1[2], not_2_out, not_1_out);
  and and_6 (out_7, not_4_out, in_1[2], not_2_out, in_1[0]);
  and and_7 (out_8, not_4_out, in_1[2], in_1[1], not_1_out);
  and and_8 (out_9, not_4_out, in_1[2], in_1[1], in_1[0]);
  and and_9 (out_10, in_1[3], not_3_out, not_2_out, not_1_out);
  and and_10 (out_11, in_1[3], not_3_out, not_2_out, in_1[0]);
  and and_11 (out_12, in_1[3], not_3_out, in_1[1], not_1_out);
  and and_12 (out_13, in_1[3], not_3_out, in_1[1], in_1[0]);
  and and_13 (out_14, in_1[3], in_1[2], not_2_out, not_1_out);
  and and_14 (out_15, in_1[3], in_1[2], not_2_out, in_1[0]);
  and and_15 (out_16, in_1[3], in_1[2], in_1[1], not_1_out);
  and and_16 (M, in_1[3], in_1[2], in_1[1], in_1[0]);

  // Notes on the sheet:
  //   out_7: pull=down
  //   M: pull=down
  //   out_5: pull=down
  //   L: pull=down
  //   out_8: pull=down
  //   out_3: pull=down
  //   out_6: pull=down
  //   out_15: pull=down
  //   out_11: pull=down
  //   in_1: pull=down
  //   out_10: pull=down
  //   out_14: pull=down
  //   out_4: pull=down
  //   out_13: pull=down
  //   out_12: pull=down
  //   out_9: pull=down
  //   out_16: pull=down
endmodule

module HALF_ADDER (
  input  in_1,
  input  in_2,
  output out_3,
  output out_4
);

  xor xor_1 (out_3, in_1, in_2);
  and and_1 (out_4, in_1, in_2);
endmodule

module FULL_ADDER (
  input  in_1,
  input  in_2,
  input  in_3,
  output out_4,
  output out_5
);

  wire half_adder_1_out_3, half_adder_1_out_4, half_adder_2_out_4;

  HALF_ADDER half_adder_1 (.in_1(in_1), .in_2(in_2), .out_3(half_adder_1_out_3), .out_4(half_adder_1_out_4));
  HALF_ADDER half_adder_2 (.in_1(half_adder_1_out_3), .in_2(in_3), .out_3(out_4), .out_4(half_adder_2_out_4));
  or or_1 (out_5, half_adder_2_out_4, half_adder_1_out_4);
endmodule

module RIPPLE_ADDER_8 (
  input  [7:0] in_1,
  input  in_2,
  input  [7:0] in_3,
  output [7:0] out_4,
  output out_5
);

  wire full_adder_1_out_5, full_adder_2_out_5, full_adder_3_out_5, full_adder_4_out_5, full_adder_5_out_5,
       full_adder_6_out_5, full_adder_7_out_5;

  FULL_ADDER full_adder_1 (.in_1(in_3[0]), .in_2(in_1[0]), .in_3(in_2), .out_4(out_4[0]), .out_5(full_adder_1_out_5));
  FULL_ADDER full_adder_2 (
    .in_1(in_3[1]), .in_2(in_1[1]), .in_3(full_adder_1_out_5), .out_4(out_4[1]), .out_5(full_adder_2_out_5));
  FULL_ADDER full_adder_3 (
    .in_1(in_3[2]), .in_2(in_1[2]), .in_3(full_adder_2_out_5), .out_4(out_4[2]), .out_5(full_adder_3_out_5));
  FULL_ADDER full_adder_4 (
    .in_1(in_3[3]), .in_2(in_1[3]), .in_3(full_adder_3_out_5), .out_4(out_4[3]), .out_5(full_adder_4_out_5));
  FULL_ADDER full_adder_5 (
    .in_1(in_3[4]), .in_2(in_1[4]), .in_3(full_adder_4_out_5), .out_4(out_4[4]), .out_5(full_adder_5_out_5));
  FULL_ADDER full_adder_6 (
    .in_1(in_3[5]), .in_2(in_1[5]), .in_3(full_adder_5_out_5), .out_4(out_4[5]), .out_5(full_adder_6_out_5));
  FULL_ADDER full_adder_7 (
    .in_1(in_3[6]), .in_2(in_1[6]), .in_3(full_adder_6_out_5), .out_4(out_4[6]), .out_5(full_adder_7_out_5));
  FULL_ADDER full_adder_8 (.in_1(in_3[7]), .in_2(in_1[7]), .in_3(full_adder_7_out_5), .out_4(out_4[7]), .out_5(out_5));
endmodule

module ALU_ADD_SUB_RIPPLE (
  input  Cin,
  input  [7:0] in_2,
  input  SUB_SIGN,
  input  [7:0] in_4,
  output [7:0] out_5,
  output out_6
);

  wire and_1_out, not_1_out, or_1_out;
  wire [7:0] xor_7_out;

  xor xor_1 (xor_7_out[7], SUB_SIGN, in_4[7]);
  xor xor_2 (xor_7_out[6], SUB_SIGN, in_4[6]);
  xor xor_3 (xor_7_out[5], SUB_SIGN, in_4[5]);
  not not_1 (not_1_out, SUB_SIGN);
  and and_1 (and_1_out, not_1_out, Cin);
  or or_1 (or_1_out, SUB_SIGN, and_1_out);
  xor xor_4 (xor_7_out[4], SUB_SIGN, in_4[4]);
  RIPPLE_ADDER_8 ripple_adder_8_1 (.in_1(xor_7_out), .in_2(or_1_out), .in_3(in_2), .out_4(out_5), .out_5(out_6));
  xor xor_5 (xor_7_out[3], SUB_SIGN, in_4[3]);
  xor xor_6 (xor_7_out[2], SUB_SIGN, in_4[2]);
  xor xor_7 (xor_7_out[0], SUB_SIGN, in_4[0]);
  xor xor_8 (xor_7_out[1], SUB_SIGN, in_4[1]);

  // Notes on the sheet:
  //   Cin: pull=down
endmodule

module ALU_SH_R (
  input  [7:0] in_1,
  input  in_2,
  output out_3,
  output [7:0] out_4
);

  wire [7:1] register_8_1_out_5;

  REGISTER_8 register_8_1 (.in_1(in_1), .in_2(1'b1), .in_3(1'b1), .out_5({register_8_1_out_5, out_3}));  // open: out_4
  REGISTER_8 register_8_2 (.in_1({in_2, register_8_1_out_5}), .in_2(1'b1), .in_3(1'b1), .out_5(out_4));  // open: out_4
endmodule

module ALU_SH_L (
  input  in_1,
  input  [7:0] in_2,
  output [7:0] out_3,
  output out_4
);

  wire [6:0] register_8_1_out_5;

  REGISTER_8 register_8_1 (.in_1(in_2), .in_2(1'b1), .in_3(1'b1), .out_5({out_4, register_8_1_out_5}));  // open: out_4
  REGISTER_8 register_8_2 (.in_1({register_8_1_out_5, in_1}), .in_2(1'b1), .in_3(1'b1), .out_5(out_3));  // open: out_4
endmodule

module ALU_XOR_COMP_1 (
  input  Prev_equal,
  input  Prev_greater,
  input  A,
  input  B,
  output Comp_res,
  output out_6,
  output Equals
);

  wire and_2_out, not_1_out;

  xor xor_1 (Comp_res, A, B);
  not not_1 (not_1_out, Comp_res);
  and and_1 (Equals, not_1_out, Prev_equal);
  and and_2 (and_2_out, A, Comp_res, Prev_equal);
  or or_1 (out_6, and_2_out, Prev_greater);
endmodule

module ALU_XOR_COMP_8 (
  input  [7:0] in_1,
  input  [7:0] in_2,
  output [7:0] out_3,
  output out_4,
  output out_5
);

  wire alu_xor_comp_1_1_equals, alu_xor_comp_1_1_out_6, alu_xor_comp_1_2_equals, alu_xor_comp_1_2_out_6,
       alu_xor_comp_1_3_equals, alu_xor_comp_1_3_out_6, alu_xor_comp_1_4_equals, alu_xor_comp_1_4_out_6,
       alu_xor_comp_1_5_equals, alu_xor_comp_1_5_out_6, alu_xor_comp_1_6_equals, alu_xor_comp_1_6_out_6,
       alu_xor_comp_1_7_equals, alu_xor_comp_1_7_out_6;

  ALU_XOR_COMP_1 alu_xor_comp_1_1 (
    .A(in_2[7]), .B(in_1[7]), .Comp_res(out_3[7]), .out_6(alu_xor_comp_1_1_out_6),
    .Equals(alu_xor_comp_1_1_equals), .Prev_equal(1'b1), .Prev_greater(1'b0));
  ALU_XOR_COMP_1 alu_xor_comp_1_2 (
    .A(in_2[6]), .B(in_1[6]), .Comp_res(out_3[6]), .out_6(alu_xor_comp_1_2_out_6),
    .Equals(alu_xor_comp_1_2_equals), .Prev_equal(alu_xor_comp_1_1_equals),
    .Prev_greater(alu_xor_comp_1_1_out_6));
  ALU_XOR_COMP_1 alu_xor_comp_1_3 (
    .A(in_2[5]), .B(in_1[5]), .Comp_res(out_3[5]), .out_6(alu_xor_comp_1_3_out_6),
    .Equals(alu_xor_comp_1_3_equals), .Prev_equal(alu_xor_comp_1_2_equals),
    .Prev_greater(alu_xor_comp_1_2_out_6));
  ALU_XOR_COMP_1 alu_xor_comp_1_4 (
    .A(in_2[4]), .B(in_1[4]), .Comp_res(out_3[4]), .out_6(alu_xor_comp_1_4_out_6),
    .Equals(alu_xor_comp_1_4_equals), .Prev_equal(alu_xor_comp_1_3_equals),
    .Prev_greater(alu_xor_comp_1_3_out_6));
  ALU_XOR_COMP_1 alu_xor_comp_1_5 (
    .A(in_2[3]), .B(in_1[3]), .Comp_res(out_3[3]), .out_6(alu_xor_comp_1_5_out_6),
    .Equals(alu_xor_comp_1_5_equals), .Prev_equal(alu_xor_comp_1_4_equals),
    .Prev_greater(alu_xor_comp_1_4_out_6));
  ALU_XOR_COMP_1 alu_xor_comp_1_6 (
    .A(in_2[2]), .B(in_1[2]), .Comp_res(out_3[2]), .out_6(alu_xor_comp_1_6_out_6),
    .Equals(alu_xor_comp_1_6_equals), .Prev_equal(alu_xor_comp_1_5_equals),
    .Prev_greater(alu_xor_comp_1_5_out_6));
  ALU_XOR_COMP_1 alu_xor_comp_1_7 (
    .A(in_2[1]), .B(in_1[1]), .Comp_res(out_3[1]), .out_6(alu_xor_comp_1_7_out_6),
    .Equals(alu_xor_comp_1_7_equals), .Prev_equal(alu_xor_comp_1_6_equals),
    .Prev_greater(alu_xor_comp_1_6_out_6));
  ALU_XOR_COMP_1 alu_xor_comp_1_8 (
    .A(in_2[0]), .B(in_1[0]), .Comp_res(out_3[0]), .out_6(out_4), .Equals(out_5),
    .Prev_equal(alu_xor_comp_1_7_equals), .Prev_greater(alu_xor_comp_1_7_out_6));
endmodule

module ALU_ZERO_FLAG (
  input  [7:0] in_1,
  output out_2
);

  nor nor_1 (out_2, in_1[0], in_1[1], in_1[2], in_1[3], in_1[4], in_1[5], in_1[6], in_1[7]);
endmodule

module ALU_AND (
  input  [7:0] in_1,
  input  [7:0] in_2,
  output [7:0] out_3
);

  and and_1 (out_3[0], in_1[0], in_2[0]);
  and and_2 (out_3[1], in_1[1], in_2[1]);
  and and_3 (out_3[2], in_1[2], in_2[2]);
  and and_4 (out_3[3], in_1[3], in_2[3]);
  and and_5 (out_3[4], in_1[4], in_2[4]);
  and and_6 (out_3[5], in_1[5], in_2[5]);
  and and_7 (out_3[6], in_1[6], in_2[6]);
  and and_8 (out_3[7], in_1[7], in_2[7]);
endmodule

module ALU_OR (
  input  [7:0] in_1,
  input  [7:0] in_2,
  output [7:0] out_3
);

  or or_1 (out_3[0], in_1[0], in_2[0]);
  or or_2 (out_3[1], in_1[1], in_2[1]);
  or or_3 (out_3[2], in_1[2], in_2[2]);
  or or_4 (out_3[3], in_1[3], in_2[3]);
  or or_5 (out_3[4], in_1[4], in_2[4]);
  or or_6 (out_3[5], in_1[5], in_2[5]);
  or or_7 (out_3[6], in_1[6], in_2[6]);
  or or_8 (out_3[7], in_1[7], in_2[7]);
endmodule

module ALU (
  input  [7:0] in_1,
  input  [7:0] in_2,
  input  in_3,
  input  [2:0] Instruction,
  output A_greater,
  output equals,
  output zero,
  output [7:0] \output ,
  output Cout
);

  wire alu_add_sub_ripple_1_out_6, alu_sh_l_1_out_4, alu_sh_r_1_out_3, and_1_out, and_2_out, and_3_out,
       decoder_1_out0, decoder_1_out1, decoder_1_out2, decoder_1_out3, decoder_1_out4, decoder_1_out5,
       decoder_1_out6, decoder_1_out7, or_1_out;
  wire [7:0] alu_add_sub_ripple_1_out_5, alu_and_1_out_3, alu_not_1_out_2, alu_or_1_out_3, alu_sh_l_1_out_3,
       alu_sh_r_1_out_4, alu_xor_comp_8_1_out_3;

  ALU_AND alu_and_1 (.in_1(in_1), .in_2(in_2), .out_3(alu_and_1_out_3));
  ALU_OR alu_or_1 (.in_1(in_1), .in_2(in_2), .out_3(alu_or_1_out_3));
  ALU_XOR_COMP_8 alu_xor_comp_8_1 (
    .in_1(in_2), .in_2(in_1), .out_3(alu_xor_comp_8_1_out_3), .out_5(equals), .out_4(A_greater));
  ALU_NOT alu_not_1 (.in_1(in_1), .out_2(alu_not_1_out_2));
  ALU_SH_L alu_sh_l_1 (.in_1(in_3), .in_2(in_1), .out_3(alu_sh_l_1_out_3), .out_4(alu_sh_l_1_out_4));
  ALU_SH_R alu_sh_r_1 (.in_1(in_1), .out_3(alu_sh_r_1_out_3), .out_4(alu_sh_r_1_out_4), .in_2(in_3));
  ALU_ADD_SUB_RIPPLE alu_add_sub_ripple_1 (
    .in_2(in_1), .SUB_SIGN(decoder_1_out1), .out_5(alu_add_sub_ripple_1_out_5),
    .out_6(alu_add_sub_ripple_1_out_6), .in_4(in_2), .Cin(in_3));
  Decoder #(.select(3), .disabled(0)) decoder_1 (
    .out0(decoder_1_out0), .out1(decoder_1_out1), .out2(decoder_1_out2), .out3(decoder_1_out3),
    .out4(decoder_1_out4), .out5(decoder_1_out5), .out6(decoder_1_out6), .out7(decoder_1_out7),
    .sel(Instruction), .en(1'b1));
  or or_1 (or_1_out, decoder_1_out0, decoder_1_out1);
  ENABLE enable_1 (.in_1(alu_xor_comp_8_1_out_3), .out_3(\output ), .in_2(decoder_1_out7));
  ENABLE enable_2 (.in_1(alu_and_1_out_3), .out_3(\output ), .in_2(decoder_1_out6));
  ENABLE enable_3 (.in_1(alu_or_1_out_3), .out_3(\output ), .in_2(decoder_1_out5));
  ENABLE enable_4 (.in_1(alu_not_1_out_2), .out_3(\output ), .in_2(decoder_1_out4));
  ENABLE enable_5 (.in_1(alu_sh_l_1_out_3), .out_3(\output ), .in_2(decoder_1_out3));
  ENABLE enable_6 (.in_1(alu_sh_r_1_out_4), .out_3(\output ), .in_2(decoder_1_out2));
  ENABLE enable_7 (.in_1(alu_add_sub_ripple_1_out_5), .out_3(\output ), .in_2(or_1_out));
  and and_1 (and_1_out, decoder_1_out3, alu_sh_l_1_out_4);
  assign Cout = decoder_1_out3 ? and_1_out : 1'bz;  // Controlled_Buffer controlled_buffer_1
  assign Cout = decoder_1_out2 ? and_2_out : 1'bz;  // Controlled_Buffer controlled_buffer_2
  and and_2 (and_2_out, decoder_1_out2, alu_sh_r_1_out_3);
  assign Cout = or_1_out ? and_3_out : 1'bz;  // Controlled_Buffer controlled_buffer_3
  and and_3 (and_3_out, or_1_out, alu_add_sub_ripple_1_out_6);
  ALU_ZERO_FLAG alu_zero_flag_1 (.in_1(\output ), .out_2(zero));

  // Notes on the sheet:
  //   in_2: pull=down
  //   Instruction: pull=down
  //   in_3: pull=down
  //   in_1: pull=down
endmodule

module ALU_NOT (
  input  [7:0] in_1,
  output [7:0] out_2
);

  not not_1 (out_2[0], in_1[0]);
  not not_2 (out_2[1], in_1[1]);
  not not_3 (out_2[2], in_1[2]);
  not not_4 (out_2[3], in_1[3]);
  not not_5 (out_2[4], in_1[4]);
  not not_6 (out_2[5], in_1[5]);
  not not_7 (out_2[6], in_1[6]);
  not not_8 (out_2[7], in_1[7]);
endmodule

module CLK (
  input  CLKin,
  output CLK,
  output CLKs,
  output CLKe
);

  wire j_k_ff_1_qn;

  J_K_Flip_Flop j_k_ff_1 (.J(1'b1), .clk(CLKin), .K(1'b1), .Q(CLK), .Qn(j_k_ff_1_qn));  // open: preset, en, reset
  and and_1 (CLKs, CLKin, CLK);
  nand nand_1 (CLKe, j_k_ff_1_qn, CLKin);
endmodule

module RAM_MEM_BYTE_CELL (
  input  [7:0] in_1,
  input  RST,
  input  H,
  input  V,
  input  S,
  input  E,
  output [7:0] out_7
);

  wire and_1_out, and_2_out, and_3_out, or_1_out;
  wire [7:0] register_8_1_out_5;

  and and_1 (and_1_out, H, V);
  and and_2 (and_2_out, and_1_out, S);
  or or_1 (or_1_out, RST, and_2_out);
  and and_3 (and_3_out, and_1_out, E);
  REGISTER_8 register_8_1 (.in_1(in_1), .in_2(or_1_out), .in_3(and_3_out), .out_5(register_8_1_out_5));  // open: out_4
  assign out_7 = and_3_out ? register_8_1_out_5 : 8'bz;  // Controlled_Buffer controlled_buffer_1
endmodule

module RAM_64 (
  input  [7:0] address,
  input  [7:0] in_2,
  input  S,
  input  STA,
  input  E,
  input  RST,
  output [7:0] out_7
);

  wire [7:0] mem_1_byte_1_out_3;

  MEM_1_BYTE mem_1_byte_1 (.in_1(address), .out_3(mem_1_byte_1_out_3), .in_2(STA));
  RAM #(.bus("separate")) ram_1 (
    .addr(mem_1_byte_1_out_3), .din(in_2), .data(out_7), .str(S), .sel(1'b1), .clk(S), .ld(E), .clr(RST));
endmodule

module CPU_BUS_1 (
  input  [7:0] in_1,
  input  in_2,
  output [7:0] out_3
);

  wire not_1_out;

  and and_1 (out_3[6], in_1[6], not_1_out);
  and and_2 (out_3[7], in_1[7], not_1_out);
  and and_3 (out_3[5], in_1[5], not_1_out);
  and and_4 (out_3[4], in_1[4], not_1_out);
  and and_5 (out_3[3], in_1[3], not_1_out);
  and and_6 (out_3[2], in_1[2], not_1_out);
  and and_7 (out_3[1], in_1[1], not_1_out);
  or or_1 (out_3[0], in_1[0], in_2);
  not not_1 (not_1_out, in_2);
endmodule

module CPU_ACC (
  input  [7:0] in_1,
  input  in_2,
  input  in_3,
  output [7:0] out_4,
  output [7:0] out_5
);

  wire [7:0] controlled_buffer_1_out, register_8_1_out_5;

  assign controlled_buffer_1_out = in_2 ? in_1 : 8'bz;  // Controlled_Buffer controlled_buffer_1
  REGISTER_8 register_8_1 (
    .in_1(controlled_buffer_1_out), .in_2(in_2), .in_3(in_3), .out_5(register_8_1_out_5), .out_4(out_5));
  assign out_4 = in_3 ? register_8_1_out_5 : 8'bz;  // Controlled_Buffer controlled_buffer_2

  // Notes on the sheet:
  //   in_1: pull=down
endmodule

module CPU_TEMP (
  input  [7:0] in_1,
  input  in_2,
  output [7:0] out_3
);

  wire [7:0] controlled_buffer_1_out;

  assign controlled_buffer_1_out = in_2 ? in_1 : 8'bz;  // Controlled_Buffer controlled_buffer_1
  MEM_1_BYTE mem_1_byte_1 (.in_1(controlled_buffer_1_out), .out_3(out_3), .in_2(in_2));

  // Notes on the sheet:
  //   in_1: pull=down
endmodule

module COUNTER_8 (
  input  in_1,
  input  in_2,
  output out_3,
  output out_4,
  output out_5,
  output out_6,
  output out_7,
  output out_8,
  output out_9
);

  wire mem_1_bit_1_out_3, mem_1_bit_2_out_3, mem_1_bit_3_out_3, mem_1_bit_4_out_3, mem_1_bit_5_out_3,
       mem_1_bit_6_out_3, mem_1_bit_7_out_3, mem_1_bit_8_out_3, mem_1_bit_9_out_3, mem_1_bit_10_out_3,
       mem_1_bit_11_out_3, not_1_out, not_2_out, not_3_out, not_4_out, not_5_out, not_6_out, not_7_out,
       not_8_out, or_1_out, or_2_out;

  not not_1 (not_1_out, in_1);
  or or_1 (or_1_out, in_1, in_2);
  not not_2 (not_2_out, in_2);
  or or_2 (or_2_out, in_1, not_2_out);
  or or_3 (out_3, in_1, not_3_out);
  not not_3 (not_3_out, mem_1_bit_2_out_3);
  MEM_1_BIT mem_1_bit_1 (.D(not_1_out), .E(or_1_out), .out_3(mem_1_bit_1_out_3));
  MEM_1_BIT mem_1_bit_2 (.D(mem_1_bit_1_out_3), .E(or_2_out), .out_3(mem_1_bit_2_out_3));
  and and_1 (out_4, mem_1_bit_2_out_3, not_4_out);
  MEM_1_BIT mem_1_bit_3 (.D(mem_1_bit_2_out_3), .E(or_1_out), .out_3(mem_1_bit_3_out_3));
  not not_4 (not_4_out, mem_1_bit_4_out_3);
  MEM_1_BIT mem_1_bit_4 (.D(mem_1_bit_3_out_3), .E(or_2_out), .out_3(mem_1_bit_4_out_3));
  and and_2 (out_5, mem_1_bit_4_out_3, not_5_out);
  MEM_1_BIT mem_1_bit_5 (.D(mem_1_bit_4_out_3), .E(or_1_out), .out_3(mem_1_bit_5_out_3));
  not not_5 (not_5_out, mem_1_bit_6_out_3);
  MEM_1_BIT mem_1_bit_6 (.D(mem_1_bit_5_out_3), .E(or_2_out), .out_3(mem_1_bit_6_out_3));
  and and_3 (out_6, mem_1_bit_6_out_3, not_6_out);
  MEM_1_BIT mem_1_bit_7 (.D(mem_1_bit_6_out_3), .E(or_1_out), .out_3(mem_1_bit_7_out_3));
  not not_6 (not_6_out, mem_1_bit_8_out_3);
  MEM_1_BIT mem_1_bit_8 (.D(mem_1_bit_7_out_3), .E(or_2_out), .out_3(mem_1_bit_8_out_3));
  and and_4 (out_7, mem_1_bit_8_out_3, not_7_out);
  not not_7 (not_7_out, mem_1_bit_10_out_3);
  MEM_1_BIT mem_1_bit_9 (.D(mem_1_bit_8_out_3), .E(or_1_out), .out_3(mem_1_bit_9_out_3));
  MEM_1_BIT mem_1_bit_10 (.D(mem_1_bit_9_out_3), .E(or_2_out), .out_3(mem_1_bit_10_out_3));
  and and_5 (out_8, mem_1_bit_10_out_3, not_8_out);
  MEM_1_BIT mem_1_bit_11 (.D(mem_1_bit_10_out_3), .E(or_1_out), .out_3(mem_1_bit_11_out_3));
  not not_8 (not_8_out, out_9);
  MEM_1_BIT mem_1_bit_12 (.D(mem_1_bit_11_out_3), .E(or_2_out), .out_3(out_9));

  // Notes on the sheet:
  //   in_1: pull=up
endmodule

module CPU (
  input  CLK,
  input  [7:0] RAM_Data_Out,
  input  in_3,
  output [7:0] R0,
  output [7:0] R1,
  output [7:0] R2,
  output [7:0] R3,
  output [7:0] RAM_Address,
  output [7:0] BUS,
  output RAM_ENABLE,
  output RAM_SET,
  output END,
  output [7:0] ACC,
  output [7:0] RAM_Data_In,
  output [7:0] IAR,
  output [7:0] IR
);

  wire alu_1_a_greater, alu_1_cout, alu_1_equals, alu_1_zero, and_1_out, and_2_out, clk_1_clk, clk_1_clke,
       clk_1_clks, cpu_carry_temp_1_out_3, cpu_flag_reg_1_out_6, cpu_flag_reg_1_out_7, cpu_flag_reg_1_out_8,
       cpu_flag_reg_1_out_9, cu_1_acce, cu_1_accs, cu_1_bus1, cu_1_flags, cu_1_iare, cu_1_iars, cu_1_irs,
       cu_1_mars, cu_1_out_21, cu_1_reg_e0, cu_1_reg_e1, cu_1_reg_e2, cu_1_reg_e3, cu_1_reg_s0, cu_1_reg_s3,
       cu_1_regs_1, cu_1_regs_2, cu_1_temps, not_1_out;
  wire [2:0] cu_1_out_31;
  wire [7:0] alu_1_output, cpu_bus_1_1_out_3, cpu_ir_1_out_4, cpu_temp_1_out_3;

  ALU alu_1 (
    .in_1(RAM_Data_Out), .in_2(cpu_bus_1_1_out_3), .in_3(and_1_out), .Instruction(cu_1_out_31),
    .A_greater(alu_1_a_greater), .equals(alu_1_equals), .zero(alu_1_zero), .\output (alu_1_output),
    .Cout(alu_1_cout));
  CPU_TEMP cpu_temp_1 (.in_1(RAM_Data_Out), .in_2(cu_1_temps), .out_3(cpu_temp_1_out_3));
  CPU_BUS_1 cpu_bus_1_1 (.in_1(cpu_temp_1_out_3), .in_2(cu_1_bus1), .out_3(cpu_bus_1_1_out_3));
  and and_1 (and_1_out, cpu_carry_temp_1_out_3, cu_1_out_21);
  CPU_ACC cpu_acc_1 (.in_1(alu_1_output), .in_2(cu_1_accs), .in_3(cu_1_acce), .out_4(RAM_Data_Out), .out_5(ACC));
  CPU_CARRY_TEMP cpu_carry_temp_1 (.in_1(cpu_flag_reg_1_out_9), .in_2(cu_1_temps), .out_3(cpu_carry_temp_1_out_3));
  CPU_FLAG_REG cpu_flag_reg_1 (
    .in_1(alu_1_a_greater), .in_2(alu_1_equals), .in_3(alu_1_zero), .in_4(alu_1_cout), .in_5(cu_1_flags),
    .out_6(cpu_flag_reg_1_out_6), .out_7(cpu_flag_reg_1_out_7), .out_8(cpu_flag_reg_1_out_8),
    .out_9(cpu_flag_reg_1_out_9));
  and and_2 (and_2_out, CLK, not_1_out);
  not not_1 (not_1_out, END);
  CPU_REG cpu_reg_1 (.in_1(RAM_Data_Out), .in_2(cu_1_reg_s0), .in_3(cu_1_reg_e0), .out_4(RAM_Data_Out), .out_5(R0));
  CLK clk_1 (.CLKin(and_2_out), .CLK(clk_1_clk), .CLKs(clk_1_clks), .CLKe(clk_1_clke));
  CU cu_1 (
    .CLK(clk_1_clk), .CLKe(clk_1_clke), .CLKs(clk_1_clks), .BUS1(cu_1_bus1), .IARe(cu_1_iare),
    .RAMe(RAM_ENABLE), .ACCe(cu_1_acce), .REG_e0(cu_1_reg_e0), .REG_e1(cu_1_reg_e1), .REG_e2(cu_1_reg_e2),
    .REG_e3(cu_1_reg_e3), .MARs(cu_1_mars), .TEMPs(cu_1_temps), .RAMs(RAM_SET), .ACCs(cu_1_accs),
    .REG_s0(cu_1_reg_s0), .REGs_1(cu_1_regs_1), .REGs_2(cu_1_regs_2), .REG_s3(cu_1_reg_s3), .IARs(cu_1_iars),
    .IRs(cu_1_irs), .in_9(cpu_ir_1_out_4), .out_31(cu_1_out_31), .gr(cpu_flag_reg_1_out_6),
    .eq(cpu_flag_reg_1_out_7), .zero(cpu_flag_reg_1_out_8), .C(cpu_flag_reg_1_out_9), .out_21(cu_1_out_21),
    .in_2(in_3), .FLAGs(cu_1_flags), .END(END));
  CPU_REG cpu_reg_2 (.in_1(RAM_Data_Out), .in_2(cu_1_regs_1), .in_3(cu_1_reg_e1), .out_4(RAM_Data_Out), .out_5(R1));
  CPU_IAR cpu_iar_1 (.in_1(RAM_Data_Out), .in_2(cu_1_iars), .in_3(cu_1_iare), .out_4(RAM_Data_Out), .out_5(IAR));
  CPU_REG cpu_reg_3 (.in_1(RAM_Data_Out), .in_2(cu_1_regs_2), .in_3(cu_1_reg_e2), .out_4(RAM_Data_Out), .out_5(R2));
  CPU_IR cpu_ir_1 (.in_1(RAM_Data_Out), .in_2(cu_1_irs), .out_4(cpu_ir_1_out_4), .DATA(IR));
  CPU_REG cpu_reg_4 (.in_1(RAM_Data_Out), .in_2(cu_1_reg_s3), .in_3(cu_1_reg_e3), .out_4(RAM_Data_Out), .out_5(R3));
  CPU_MAR cpu_mar_1 (.in_1(RAM_Data_Out), .in_2(cu_1_mars), .out_3(RAM_Address));

  assign BUS = RAM_Data_Out;
  assign RAM_Data_In = RAM_Data_Out;
endmodule

module CPU_REG (
  input  [7:0] in_1,
  input  in_2,
  input  in_3,
  output [7:0] out_4,
  output [7:0] out_5
);

  wire [7:0] controlled_buffer_1_out, register_8_1_out_5;

  assign controlled_buffer_1_out = in_2 ? in_1 : 8'bz;  // Controlled_Buffer controlled_buffer_1
  REGISTER_8 register_8_1 (
    .in_1(controlled_buffer_1_out), .in_2(in_2), .in_3(in_3), .out_5(register_8_1_out_5), .out_4(out_5));
  assign out_4 = in_3 ? register_8_1_out_5 : 8'bz;  // Controlled_Buffer controlled_buffer_2

  // Notes on the sheet:
  //   in_2: pull=up
  //   in_1: pull=down
endmodule

module CPU_template (
  input  [2:0] in_1
);

  wire clk_1_clk, clk_1_clke, clk_1_clks, clock_1_out;
  wire [7:0] alu_1_output, cpu_acc_1_out_4, cpu_bus_1_1_out_3, cpu_temp_1_out_3;

  ALU alu_1 (
    .in_1({cpu_acc_1_out_4[7:2], cpu_acc_1_out_4[4], cpu_acc_1_out_4[0]}), .in_2(cpu_bus_1_1_out_3),
    .in_3(1'b0), .Instruction(in_1), .\output (alu_1_output));  // open: A_greater, equals, zero, Cout
  CPU_TEMP cpu_temp_1 (
    .in_1({cpu_acc_1_out_4[7:2], cpu_acc_1_out_4[4], cpu_acc_1_out_4[0]}), .out_3(cpu_temp_1_out_3));  // open: in_2
  CPU_BUS_1 cpu_bus_1_1 (.in_1(cpu_temp_1_out_3), .out_3(cpu_bus_1_1_out_3));  // open: in_2
  CPU_ACC cpu_acc_1 (
    .in_1(alu_1_output), .out_4({cpu_acc_1_out_4[7:2], cpu_acc_1_out_4[4], cpu_acc_1_out_4[0]}));  // open: in_2, in_3, out_5
  Clock clock_1 (.out(clock_1_out));
  CLK clk_1 (.CLKin(clock_1_out), .CLK(clk_1_clk), .CLKs(clk_1_clks), .CLKe(clk_1_clke));
  CPU_REG cpu_reg_1 (
    .in_1({cpu_acc_1_out_4[7:2], cpu_acc_1_out_4[4], cpu_acc_1_out_4[0]}),
    .out_4({cpu_acc_1_out_4[7:2], cpu_acc_1_out_4[4], cpu_acc_1_out_4[0]}));  // open: in_2, in_3, out_5
  CPU_REG cpu_reg_2 (
    .in_1({cpu_acc_1_out_4[7:2], cpu_acc_1_out_4[4], cpu_acc_1_out_4[0]}),
    .out_4({cpu_acc_1_out_4[7:2], cpu_acc_1_out_4[4], cpu_acc_1_out_4[0]}));  // open: in_2, in_3, out_5
  CPU_REG cpu_reg_3 (
    .in_1({cpu_acc_1_out_4[7:2], cpu_acc_1_out_4[4], cpu_acc_1_out_4[0]}),
    .out_4({cpu_acc_1_out_4[7:2], cpu_acc_1_out_4[4], cpu_acc_1_out_4[0]}));  // open: in_2, in_3, out_5
  CPU_REG cpu_reg_4 (
    .in_1({cpu_acc_1_out_4[7:2], cpu_acc_1_out_4[4], cpu_acc_1_out_4[0]}),
    .out_4({cpu_acc_1_out_4[7:2], cpu_acc_1_out_4[4], cpu_acc_1_out_4[0]}));  // open: in_2, in_3, out_5
  RAM_64 ram_64_1 ();  // open: address, STA, S, E, RST, in_2, out_7
endmodule

module CU_ADD (
  input  CLK,
  input  CLKe,
  input  CLKs,
  input  [7:0] in_4,
  output MARs,
  output BUS1,
  output TEMPs,
  output IARe,
  output RAMs,
  output RAMe,
  output ACCs,
  output ACCe,
  output REG_s0,
  output REG_e0,
  output REGs_1,
  output REG_e1,
  output REGs_2,
  output REG_e2,
  output REG_s3,
  output REG_e3,
  output IARs,
  output IRs
);

  wire counter_8_1_p3, counter_8_1_p4, counter_8_1_p5;

  and and_1 (IARe, CLKe, BUS1);
  and and_2 (RAMe, CLKe, counter_8_1_p3);
  and and_3 (ACCe, CLKe, counter_8_1_p4);
  and and_4 (REG_e0, CLKe, 1'b0);
  and and_5 (REG_e1, CLKe, 1'b0);
  and and_6 (REG_e2, CLKe, 1'b0);
  and and_7 (REG_e3, CLKe, 1'b0);
  // COUNTER_8 counter_8_1: pin names not known; wires that end beside it: CLK, BUS1, counter_8_1_p3, counter_8_1_p4, counter_8_1_p5
  and and_8 (MARs, CLKs, BUS1);
  buf and_9 (TEMPs, CLKs);  // AND_Gate
  and and_10 (RAMs, CLKs, 1'b0);
  and and_11 (ACCs, CLKs, BUS1);
  and and_12 (REG_s0, CLKs, 1'b0);
  and and_13 (REGs_1, CLKs, 1'b0);
  and and_14 (REGs_2, CLKs, 1'b0);
  and and_15 (REG_s3, CLKs, 1'b0);
  and and_16 (IARs, CLKs, counter_8_1_p4);
  and and_17 (IRs, CLKs, counter_8_1_p3);
endmodule

module CPU_IAR (
  input  [7:0] in_1,
  input  in_2,
  input  in_3,
  output [7:0] out_4,
  output [7:0] out_5
);

  REGISTER_8 register_8_1 (.in_1(in_1), .in_2(in_2), .in_3(in_3), .out_5(out_4), .out_4(out_5));

  // Notes on the sheet:
  //   in_1: pull=down
endmodule

module CPU_IR (
  input  [7:0] in_1,
  input  in_2,
  output [7:0] DATA,
  output [7:0] out_4
);

  MEM_1_BYTE mem_1_byte_1 (.in_1(in_1), .out_3(DATA), .in_2(in_2));

  assign out_4 = DATA;

  // Notes on the sheet:
  //   in_1: pull=down
endmodule

module CPU_MAR (
  input  [7:0] in_1,
  input  in_2,
  output [7:0] out_3
);

  MEM_1_BYTE mem_1_byte_1 (.in_1(in_1), .out_3(out_3), .in_2(in_2));

  // Notes on the sheet:
  //   in_1: pull=down
endmodule

module CU (
  input  CLK,
  input  in_2,
  input  CLKe,
  input  CLKs,
  input  gr,
  input  eq,
  input  zero,
  input  C,
  input  [7:0] in_9,
  output MARs,
  output BUS1,
  output IARe,
  output TEMPs,
  output RAMs,
  output ACCs,
  output IARs,
  output RAMe,
  output IRs,
  output FLAGs,
  output ACCe,
  output out_21,
  output REG_s0,
  output REGs_1,
  output REGs_2,
  output REG_e0,
  output REG_s3,
  output REG_e1,
  output REG_e2,
  output REG_e3,
  output END,
  output [2:0] out_31
);

  wire ACC_E_ALU, ACC_E_DT, ACC_E_JMPI, ACC_S_DT, ACC_S_JMPI, ALU_OP_SIGNAL, and_4_out, and_5_out, and_6_out,
       and_7_out, and_8_out, and_9_out, and_10_out, and_11_out, and_15_out, and_16_out, and_17_out,
       and_18_out, and_19_out, and_20_out, and_21_out, and_30_out, and_31_out, and_32_out, and_33_out,
       and_44_out, and_45_out, and_46_out, and_47_out, and_48_out, and_49_out, and_50_out, and_51_out,
       and_52_out, and_53_out, and_54_out, BUS_CLRF, counter_8_1_out_3, counter_8_1_out_4, counter_8_1_out_5,
       counter_8_1_out_6, counter_8_1_out_8, counter_8_1_out_9, cu_decoder_2x4_east_1_out_3,
       cu_decoder_2x4_east_1_out_4, cu_decoder_2x4_east_1_out_5, cu_decoder_2x4_east_1_out_6, decoder_1_out0,
       decoder_1_out1, decoder_1_out2, decoder_1_out3, decoder_1_out4, decoder_1_out5, decoder_1_out6,
       decoder_1_out7, IAR_E_JMPA, IAR_S_JMPA, IAR_S_JMPI1, IAR_S_JMPR, MAR_S_LD_STR, not_1_out, not_2_out,
       not_3_out, or_6_out, or_7_out, or_8_out, or_9_out, or_10_out, or_11_out, or_12_out, or_13_out,
       or_14_out, or_15_out, or_16_out, or_17_out, RAM_E_DT, RAM_E_LD, RAM_S_STR, REG_A_out_3, REG_A_out_4,
       REG_A_out_5, REG_A_out_6, REG_B_E_ALU, REG_B_out_3, REG_B_out_4, REG_B_out_5, REG_B_out_6;

  or or_1 (REG_e3, and_7_out, and_11_out);
  or or_2 (REG_e0, and_4_out, and_8_out);
  or or_3 (REG_e1, and_5_out, and_9_out);
  or or_4 (REG_e2, and_6_out, and_10_out);
  and and_1 (IARe, CLKe, or_6_out);
  and and_2 (RAMe, CLKe, or_7_out);
  and and_3 (ACCe, CLKe, or_8_out);
  and and_4 (and_4_out, CLKe, or_9_out, REG_B_out_3);
  and and_5 (and_5_out, CLKe, or_9_out, REG_B_out_4);
  and and_6 (and_6_out, CLKe, or_9_out, REG_B_out_5);
  and and_7 (and_7_out, CLKe, or_9_out, REG_B_out_6);
  or or_5 (BUS1, counter_8_1_out_3, ACC_S_JMPI, ACC_S_DT, BUS_CLRF);
  or or_6 (or_6_out, counter_8_1_out_3, IAR_E_JMPA, ACC_S_DT, ACC_S_JMPI);
  or or_7 (or_7_out, counter_8_1_out_4, IAR_S_JMPA, RAM_E_LD, RAM_E_DT, IAR_S_JMPI1);
  or or_8 (or_8_out, counter_8_1_out_5, ACC_E_DT, ACC_E_ALU, ACC_E_JMPI);
  and and_8 (and_8_out, CLKe, or_10_out, REG_A_out_3);
  and and_9 (and_9_out, CLKe, or_10_out, REG_A_out_4);
  and and_10 (and_10_out, CLKe, or_10_out, REG_A_out_5);
  and and_11 (and_11_out, CLKe, or_10_out, REG_A_out_6);
  and and_12 (out_31[2], ALU_OP_SIGNAL, in_9[6], in_9[7]);
  and and_13 (out_31[1], ALU_OP_SIGNAL, in_9[5], in_9[7]);
  and and_14 (out_31[0], ALU_OP_SIGNAL, in_9[4], in_9[7]);
  Decoder #(.select(3), .enable("false")) decoder_1 (
    .out0(decoder_1_out0), .out1(decoder_1_out1), .out2(decoder_1_out2), .out3(decoder_1_out3),
    .out4(decoder_1_out4), .out5(decoder_1_out5), .out6(decoder_1_out6), .out7(decoder_1_out7),
    .sel(in_9[6:4]));
  or or_9 (or_9_out, RAM_S_STR, IAR_S_JMPR, REG_B_E_ALU);
  or or_10 (or_10_out, MAR_S_LD_STR, out_21);
  not not_1 (not_1_out, in_9[7]);
  CU_DECODER_2X4 REG_B (
    .in_1(in_9[0]), .in_2(in_9[1]), .out_3(REG_B_out_3), .out_4(REG_B_out_4), .out_5(REG_B_out_5),
    .out_6(REG_B_out_6));
  CU_DECODER_2X4 REG_A (
    .in_1(in_9[2]), .in_2(in_9[3]), .out_3(REG_A_out_3), .out_4(REG_A_out_4), .out_5(REG_A_out_5),
    .out_6(REG_A_out_6));
  and and_15 (and_15_out, decoder_1_out0, not_1_out);
  and and_16 (and_16_out, decoder_1_out1, not_1_out);
  and and_17 (and_17_out, decoder_1_out2, not_1_out);
  and and_18 (and_18_out, decoder_1_out3, not_1_out);
  and and_19 (and_19_out, decoder_1_out4, not_1_out);
  and and_20 (and_20_out, decoder_1_out5, not_1_out);
  and and_21 (and_21_out, decoder_1_out6, not_1_out);
  // AND_Gate and_22 has open pins: in0=decoder_1_out7, in1=not_1_out, out=open
  COUNTER_8 counter_8_1 (
    .in_2(CLK), .out_3(counter_8_1_out_3), .out_4(counter_8_1_out_4), .out_5(counter_8_1_out_5),
    .out_6(counter_8_1_out_6), .out_7(ALU_OP_SIGNAL), .out_8(counter_8_1_out_8), .out_9(counter_8_1_out_9),
    .in_1(counter_8_1_out_9));
  or or_11 (or_11_out, and_15_out, and_16_out);
  and and_23 (BUS_CLRF, and_21_out, counter_8_1_out_6);
  and and_24 (MAR_S_LD_STR, or_11_out, counter_8_1_out_6);
  and and_25 (ACC_S_DT, and_17_out, counter_8_1_out_6);
  and and_26 (IAR_S_JMPR, and_18_out, counter_8_1_out_6);
  and and_27 (IAR_E_JMPA, and_19_out, counter_8_1_out_6);
  and and_28 (ACC_S_JMPI, and_20_out, counter_8_1_out_6);
  and and_29 (REG_B_E_ALU, counter_8_1_out_6, in_9[7]);
  and and_30 (and_30_out, gr, in_9[3]);
  and and_31 (and_31_out, eq, in_9[2]);
  and and_32 (and_32_out, zero, in_9[1]);
  and and_33 (and_33_out, C, in_9[0]);
  not not_2 (not_2_out, in_9[5]);
  and and_34 (IAR_S_JMPA, and_19_out, ALU_OP_SIGNAL);
  and and_35 (ACC_E_JMPI, and_20_out, ALU_OP_SIGNAL);
  not not_3 (not_3_out, in_9[4]);
  and and_36 (out_21, ALU_OP_SIGNAL, in_9[7]);
  and and_37 (RAM_E_LD, and_15_out, ALU_OP_SIGNAL);
  and and_38 (RAM_S_STR, and_16_out, ALU_OP_SIGNAL);
  and and_39 (RAM_E_DT, and_17_out, ALU_OP_SIGNAL);
  or or_12 (or_12_out, and_30_out, and_31_out, and_32_out, and_33_out);
  and and_40 (ACC_E_ALU, counter_8_1_out_8, in_9[7]);
  and and_41 (ACC_E_DT, and_17_out, counter_8_1_out_8);
  and and_42 (IAR_S_JMPI1, and_20_out, counter_8_1_out_8, or_12_out);
  and and_43 (END, in_9[7], in_9[6], not_2_out, not_3_out, in_9[3], in_9[2], in_9[1], in_9[0]);
  CU_DECODER_2X4_EAST cu_decoder_2x4_east_1 (
    .in_1(in_9[0]), .in_2(in_9[1]), .out_3(cu_decoder_2x4_east_1_out_3), .out_4(cu_decoder_2x4_east_1_out_4),
    .out_5(cu_decoder_2x4_east_1_out_5), .out_6(cu_decoder_2x4_east_1_out_6));
  or or_13 (or_13_out, RAM_E_DT, RAM_E_LD, ACC_E_ALU);
  and and_44 (and_44_out, CLKs, or_14_out);
  or or_14 (or_14_out, counter_8_1_out_3, MAR_S_LD_STR, ACC_S_DT, IAR_E_JMPA, ACC_S_JMPI);
  or or_15 (or_15_out, counter_8_1_out_3, out_21, ACC_S_DT, ACC_S_JMPI);
  or or_16 (or_16_out, counter_8_1_out_5, IAR_S_JMPA, IAR_S_JMPR, ACC_E_DT, IAR_S_JMPI1, ACC_E_JMPI);
  or or_17 (or_17_out, out_21, BUS_CLRF);
  and and_45 (and_45_out, CLKs, cu_decoder_2x4_east_1_out_3, or_13_out);
  and and_46 (and_46_out, CLKs, cu_decoder_2x4_east_1_out_4, or_13_out);
  and and_47 (and_47_out, CLKs, cu_decoder_2x4_east_1_out_5, or_13_out);
  and and_48 (and_48_out, CLKs, cu_decoder_2x4_east_1_out_6, or_13_out);
  and and_49 (and_49_out, CLKs, REG_B_E_ALU);
  and and_50 (and_50_out, CLKs, RAM_S_STR);
  and and_51 (and_51_out, CLKs, or_15_out);
  and and_52 (and_52_out, CLKs, or_16_out);
  and and_53 (and_53_out, CLKs, counter_8_1_out_4);
  and and_54 (and_54_out, CLKs, or_17_out);
  or or_18 (MARs, in_2, and_44_out);
  or or_19 (TEMPs, in_2, and_49_out);
  or or_20 (RAMs, in_2, and_50_out);
  or or_21 (ACCs, in_2, and_51_out);
  or or_22 (IARs, in_2, and_52_out);
  or or_23 (IRs, in_2, and_53_out);
  or or_24 (FLAGs, in_2, and_54_out);
  or or_25 (REG_s0, in_2, and_45_out);
  or or_26 (REGs_1, in_2, and_46_out);
  or or_27 (REGs_2, in_2, and_47_out);
  or or_28 (REG_s3, in_2, and_48_out);

  // Other names for the same wires on the sheet: FLAG_S_CLRF = BUS_CLRF; IAR_S_DT = ACC_E_DT; IAR_S_JMPI = ACC_E_JMPI;
  //   BUS_DT = ACC_S_DT; IAR_E_DT = ACC_S_DT; MAR_S_DT = ACC_S_DT; MAR_S_JMPA = IAR_E_JMPA; BUS_JMPI = ACC_S_JMPI;
  //   IAR_E_JMPI = ACC_S_JMPI; MAR_S_JMPI = ACC_S_JMPI; RAM_E_JMPA = IAR_S_JMPA; RAM_E_JMPI = IAR_S_JMPI1;
  //   REB_B_E_JMPR = IAR_S_JMPR; ACC_S_ALU = out_21; FLAG_S_ALU = out_21; REG_A_E_ALU = out_21;
  //   REG_A_E_LD_STR = MAR_S_LD_STR; REG_B_E_STR = RAM_S_STR; REG_B_S_ALU = ACC_E_ALU; REG_B_S_DT = RAM_E_DT;
  //   REG_B_S_LD = RAM_E_LD; TEMP_S_ALU = REG_B_E_ALU

  // Notes on the sheet:
  //   ALU_LINE
endmodule

module CU_DECODER_2X4 (
  input  in_1,
  input  in_2,
  output out_3,
  output out_4,
  output out_5,
  output out_6
);

  Decoder #(.select(2), .enable("false")) decoder_1 (
    .out0(out_3), .out1(out_4), .out2(out_5), .out3(out_6), .sel({in_2, in_1}));
endmodule

module CU_DECODER_2X4_EAST (
  input  in_1,
  input  in_2,
  output out_3,
  output out_4,
  output out_5,
  output out_6
);

  Decoder #(.select(2), .enable("false")) decoder_1 (
    .out0(out_3), .out1(out_4), .out2(out_5), .out3(out_6), .sel({in_2, in_1}));
endmodule

module CPU_FLAG_REG (
  input  in_1,
  input  in_2,
  input  in_3,
  input  in_4,
  input  in_5,
  output out_6,
  output out_7,
  output out_8,
  output out_9
);

  MEM_1_BIT mem_1_bit_1 (.D(in_1), .E(in_5), .out_3(out_6));
  MEM_1_BIT mem_1_bit_2 (.D(in_2), .E(in_5), .out_3(out_7));
  MEM_1_BIT mem_1_bit_3 (.D(in_3), .E(in_5), .out_3(out_8));
  MEM_1_BIT mem_1_bit_4 (.D(in_4), .E(in_5), .out_3(out_9));

  // Notes on the sheet:
  //   in_4: pull=down
  //   in_1: pull=down
  //   in_3: pull=down
  //   in_2: pull=down
endmodule

module CPU_CARRY_TEMP (
  input  in_1,
  input  in_2,
  output out_3
);

  MEM_1_BIT mem_1_bit_1 (.D(in_1), .E(in_2), .out_3(out_3));

  // Notes on the sheet:
  //   in_1: pull=down
endmodule

module BIN_TO_BCD (
  input  [7:0] binary,
  output [3:0] hundreds,
  output [3:0] tens,
  output [3:0] units
);

  wire and_1_out, and_2_out, and_3_out, and_4_out, and_5_out, and_6_out, and_7_out, and_8_out, and_9_out,
       and_10_out, and_11_out, and_12_out, and_13_out, and_14_out, and_15_out, and_16_out, and_17_out,
       and_18_out, and_19_out, and_20_out, and_21_out, and_22_out, and_23_out, and_24_out, and_25_out,
       and_26_out, and_27_out, and_28_out, and_29_out, and_30_out, and_31_out, and_32_out, and_33_out,
       and_34_out, and_35_out, and_36_out, and_37_out, and_38_out, and_39_out, and_40_out, and_41_out,
       and_42_out, and_43_out, and_44_out, and_45_out, and_46_out, and_47_out, and_48_out, and_49_out,
       and_50_out, and_51_out, and_52_out, and_53_out, and_54_out, and_55_out, and_56_out, and_57_out,
       and_58_out, and_59_out, and_60_out, and_61_out, and_62_out, and_63_out, and_64_out, and_65_out,
       and_66_out, and_67_out, and_68_out, and_69_out, and_70_out, and_71_out, and_72_out, and_73_out,
       and_74_out, and_75_out, and_76_out, and_77_out, and_78_out, and_79_out, and_80_out, and_81_out,
       and_82_out, and_83_out, and_84_out, and_85_out, and_86_out, and_87_out, and_88_out, and_89_out,
       and_90_out, and_91_out, and_92_out, and_93_out, and_94_out, and_95_out, and_96_out, and_97_out,
       and_98_out, and_99_out, and_100_out, and_101_out, and_102_out, and_103_out, and_104_out, and_105_out,
       and_106_out, and_107_out, and_108_out, and_109_out, and_110_out, and_111_out, and_112_out,
       and_113_out, and_114_out, and_115_out, and_116_out, and_117_out, and_118_out, and_119_out,
       and_120_out, and_121_out, and_122_out, and_123_out, and_124_out, and_125_out, and_126_out,
       and_127_out, and_128_out, and_129_out, and_130_out, and_131_out, and_132_out, and_133_out,
       and_134_out, and_135_out, and_136_out, and_137_out, and_138_out, and_139_out, and_140_out,
       and_141_out, and_142_out, and_143_out, and_144_out, and_145_out, and_146_out, and_147_out,
       and_148_out, and_149_out, and_150_out, and_151_out, and_152_out, and_153_out, and_154_out,
       and_155_out, and_156_out, not_1_out, not_2_out, not_3_out, not_4_out, not_5_out, not_6_out, not_7_out,
       not_8_out, not_9_out, not_10_out, not_11_out, not_12_out, not_13_out, not_14_out, not_15_out,
       not_16_out, not_17_out, not_18_out, not_19_out, not_20_out, not_21_out, not_22_out, not_23_out,
       not_24_out, not_25_out, not_26_out, not_27_out, not_28_out, not_29_out, not_30_out, not_31_out,
       not_32_out, not_33_out, not_34_out, not_35_out, not_36_out, not_37_out, not_38_out, not_39_out,
       not_40_out, not_41_out, not_42_out, not_43_out, not_44_out, not_45_out, not_46_out, not_47_out,
       not_48_out, not_49_out, not_50_out, not_51_out, not_52_out, not_53_out, not_54_out, not_55_out,
       not_56_out, not_57_out, not_58_out, not_59_out, not_60_out, not_61_out, not_62_out, not_63_out,
       not_64_out, not_65_out, not_66_out, not_67_out, not_68_out, not_69_out, not_70_out, not_71_out,
       not_72_out, not_73_out, not_74_out, not_75_out, not_76_out, not_77_out, not_78_out, not_79_out,
       not_80_out, not_81_out, not_82_out, not_83_out, not_84_out, not_85_out, not_86_out, not_87_out,
       not_88_out, not_89_out, not_90_out, not_91_out, not_92_out, not_93_out, not_94_out, not_95_out,
       not_96_out, not_97_out, not_98_out, not_99_out, not_100_out, not_101_out, not_102_out, not_103_out,
       not_104_out, not_105_out, not_106_out, not_107_out, not_108_out, not_109_out, not_110_out,
       not_111_out, not_112_out, not_113_out, not_114_out, not_115_out, not_116_out, not_117_out,
       not_118_out, not_119_out, not_120_out, not_121_out, not_122_out, not_123_out, not_124_out,
       not_125_out, not_126_out, not_127_out, not_128_out, not_129_out, not_130_out, not_131_out,
       not_132_out, not_133_out, not_134_out, not_135_out, not_136_out, not_137_out, not_138_out,
       not_139_out, not_140_out, not_141_out, not_142_out, not_143_out, not_144_out, not_145_out,
       not_146_out, not_147_out, not_148_out, not_149_out, not_150_out, not_151_out, not_152_out,
       not_153_out, not_154_out, not_155_out, not_156_out, not_157_out, not_158_out, not_159_out,
       not_160_out, not_161_out, not_162_out, not_163_out, not_164_out, not_165_out, not_166_out,
       not_167_out, not_168_out, not_169_out, not_170_out, not_171_out, not_172_out, not_173_out,
       not_174_out, not_175_out, not_176_out, not_177_out, not_178_out, not_179_out, not_180_out,
       not_181_out, not_182_out, not_183_out, not_184_out, not_185_out, not_186_out, not_187_out,
       not_188_out, not_189_out, not_190_out, not_191_out, not_192_out, not_193_out, not_194_out,
       not_195_out, not_196_out, not_197_out, not_198_out, not_199_out, not_200_out, not_201_out,
       not_202_out, not_203_out, not_204_out, not_205_out, not_206_out, not_207_out, not_208_out,
       not_209_out, not_210_out, not_211_out, not_212_out, not_213_out, not_214_out, not_215_out,
       not_216_out, not_217_out, not_218_out, not_219_out, not_220_out, not_221_out, not_222_out,
       not_223_out, not_224_out, not_225_out, not_226_out, not_227_out, not_228_out, not_229_out,
       not_230_out, not_231_out, not_232_out, not_233_out, not_234_out, not_235_out, not_236_out,
       not_237_out, not_238_out, not_239_out, not_240_out, not_241_out, not_242_out, not_243_out,
       not_244_out, not_245_out, not_246_out, not_247_out, not_248_out, not_249_out, not_250_out,
       not_251_out, not_252_out, not_253_out, not_254_out, not_255_out, not_256_out, not_257_out,
       not_258_out, not_259_out, not_260_out, not_261_out, not_262_out, not_263_out, not_264_out,
       not_265_out, not_266_out, not_267_out, not_268_out, not_269_out, not_270_out, not_271_out,
       not_272_out, not_273_out, not_274_out, not_275_out, not_276_out, not_277_out, not_278_out,
       not_279_out, not_280_out, not_281_out, not_282_out, not_283_out, not_284_out, not_285_out,
       not_286_out, not_287_out, not_288_out, not_289_out, not_290_out, not_291_out, not_292_out,
       not_293_out, not_294_out, not_295_out, not_296_out, not_297_out, not_298_out, not_299_out,
       not_300_out, not_301_out, not_302_out, not_303_out, not_304_out, not_305_out, not_306_out,
       not_307_out, not_308_out, not_309_out, not_310_out, not_311_out, not_312_out, not_313_out,
       not_314_out, not_315_out, not_316_out, not_317_out, not_318_out, not_319_out, not_320_out,
       not_321_out, not_322_out, not_323_out, not_324_out, not_325_out, not_326_out, not_327_out,
       not_328_out, not_329_out, not_330_out, not_331_out, not_332_out, not_333_out, not_334_out,
       not_335_out, not_336_out, not_337_out, not_338_out, not_339_out, not_340_out, not_341_out,
       not_342_out, not_343_out, not_344_out, not_345_out, not_346_out, not_347_out, not_348_out,
       not_349_out, not_350_out, not_351_out, not_352_out, not_353_out, not_354_out, not_355_out,
       not_356_out, not_357_out, not_358_out, not_359_out, not_360_out, not_361_out, not_362_out,
       not_363_out, not_364_out, not_365_out, not_366_out, not_367_out, not_368_out, not_369_out,
       not_370_out, not_371_out, not_372_out, not_373_out, not_374_out, not_375_out, not_376_out,
       not_377_out, not_378_out, not_379_out, not_380_out, not_381_out, not_382_out, not_383_out,
       not_384_out, not_385_out, not_386_out, not_387_out, not_388_out, not_389_out, not_390_out,
       not_391_out, not_392_out, not_393_out, not_394_out, not_395_out, not_396_out, not_397_out,
       not_398_out, not_399_out, not_400_out, not_401_out, not_402_out, not_403_out, not_404_out,
       not_405_out, not_406_out, not_407_out, not_408_out, not_409_out, not_410_out, not_411_out,
       not_412_out, not_413_out, not_414_out, not_415_out, not_416_out, not_417_out, not_418_out,
       not_419_out, not_420_out, not_421_out, not_422_out, not_423_out, not_424_out, not_425_out,
       not_426_out, not_427_out, or_6_out, or_7_out, or_8_out, or_9_out;

  and and_1 (and_1_out, binary[7], binary[6], binary[3]);
  and and_2 (and_2_out, binary[7], binary[6], binary[4]);
  and and_3 (and_3_out, binary[7], binary[6], binary[5]);
  not not_1 (not_1_out, binary[7]);
  not not_2 (not_2_out, binary[7]);
  not not_3 (not_3_out, binary[7]);
  not not_4 (not_4_out, binary[6]);
  not not_5 (not_5_out, binary[5]);
  not not_6 (not_6_out, binary[4]);
  not not_7 (not_7_out, binary[3]);
  not not_8 (not_8_out, binary[7]);
  not not_9 (not_9_out, binary[5]);
  not not_10 (not_10_out, binary[7]);
  not not_11 (not_11_out, binary[4]);
  not not_12 (not_12_out, binary[3]);
  not not_13 (not_13_out, binary[2]);
  not not_14 (not_14_out, binary[6]);
  not not_15 (not_15_out, binary[6]);
  not not_16 (not_16_out, binary[5]);
  not not_17 (not_17_out, binary[4]);
  not not_18 (not_18_out, binary[3]);
  not not_19 (not_19_out, binary[6]);
  not not_20 (not_20_out, binary[4]);
  not not_21 (not_21_out, binary[7]);
  not not_22 (not_22_out, binary[6]);
  not not_23 (not_23_out, binary[7]);
  not not_24 (not_24_out, binary[5]);
  not not_25 (not_25_out, binary[4]);
  not not_26 (not_26_out, binary[6]);
  not not_27 (not_27_out, binary[4]);
  not not_28 (not_28_out, binary[6]);
  not not_29 (not_29_out, binary[5]);
  not not_30 (not_30_out, binary[6]);
  not not_31 (not_31_out, binary[4]);
  not not_32 (not_32_out, binary[6]);
  not not_33 (not_33_out, binary[3]);
  not not_34 (not_34_out, binary[2]);
  not not_35 (not_35_out, binary[7]);
  not not_36 (not_36_out, binary[6]);
  not not_37 (not_37_out, binary[5]);
  not not_38 (not_38_out, binary[7]);
  not not_39 (not_39_out, binary[6]);
  not not_40 (not_40_out, binary[5]);
  not not_41 (not_41_out, binary[7]);
  not not_42 (not_42_out, binary[6]);
  not not_43 (not_43_out, binary[6]);
  not not_44 (not_44_out, binary[4]);
  not not_45 (not_45_out, binary[3]);
  not not_46 (not_46_out, binary[7]);
  not not_47 (not_47_out, binary[5]);
  not not_48 (not_48_out, binary[4]);
  not not_49 (not_49_out, binary[7]);
  not not_50 (not_50_out, binary[6]);
  not not_51 (not_51_out, binary[4]);
  not not_52 (not_52_out, binary[3]);
  not not_53 (not_53_out, binary[6]);
  not not_54 (not_54_out, binary[4]);
  not not_55 (not_55_out, binary[2]);
  not not_56 (not_56_out, binary[6]);
  not not_57 (not_57_out, binary[3]);
  not not_58 (not_58_out, binary[2]);
  not not_59 (not_59_out, binary[4]);
  not not_60 (not_60_out, binary[5]);
  not not_61 (not_61_out, binary[7]);
  not not_62 (not_62_out, binary[5]);
  not not_63 (not_63_out, binary[4]);
  not not_64 (not_64_out, binary[7]);
  not not_65 (not_65_out, binary[5]);
  not not_66 (not_66_out, binary[4]);
  not not_67 (not_67_out, binary[7]);
  not not_68 (not_68_out, binary[5]);
  not not_69 (not_69_out, binary[7]);
  not not_70 (not_70_out, binary[6]);
  not not_71 (not_71_out, binary[5]);
  not not_72 (not_72_out, binary[3]);
  not not_73 (not_73_out, binary[2]);
  not not_74 (not_74_out, binary[7]);
  not not_75 (not_75_out, binary[6]);
  not not_76 (not_76_out, binary[4]);
  not not_77 (not_77_out, binary[3]);
  not not_78 (not_78_out, binary[7]);
  not not_79 (not_79_out, binary[6]);
  not not_80 (not_80_out, binary[3]);
  not not_81 (not_81_out, binary[7]);
  not not_82 (not_82_out, binary[3]);
  not not_83 (not_83_out, binary[7]);
  not not_84 (not_84_out, binary[6]);
  not not_85 (not_85_out, binary[2]);
  not not_86 (not_86_out, binary[5]);
  not not_87 (not_87_out, binary[4]);
  not not_88 (not_88_out, binary[3]);
  not not_89 (not_89_out, binary[7]);
  not not_90 (not_90_out, binary[5]);
  not not_91 (not_91_out, binary[4]);
  not not_92 (not_92_out, binary[7]);
  not not_93 (not_93_out, binary[5]);
  not not_94 (not_94_out, binary[7]);
  not not_95 (not_95_out, binary[5]);
  not not_96 (not_96_out, binary[7]);
  not not_97 (not_97_out, binary[4]);
  not not_98 (not_98_out, binary[7]);
  not not_99 (not_99_out, binary[3]);
  not not_100 (not_100_out, binary[2]);
  not not_101 (not_101_out, binary[5]);
  not not_102 (not_102_out, binary[4]);
  not not_103 (not_103_out, binary[3]);
  not not_104 (not_104_out, binary[5]);
  not not_105 (not_105_out, binary[4]);
  not not_106 (not_106_out, binary[3]);
  not not_107 (not_107_out, binary[5]);
  not not_108 (not_108_out, binary[3]);
  not not_109 (not_109_out, binary[6]);
  not not_110 (not_110_out, binary[5]);
  not not_111 (not_111_out, binary[2]);
  not not_112 (not_112_out, binary[6]);
  not not_113 (not_113_out, binary[5]);
  not not_114 (not_114_out, binary[5]);
  not not_115 (not_115_out, binary[2]);
  not not_116 (not_116_out, binary[4]);
  not not_117 (not_117_out, binary[4]);
  not not_118 (not_118_out, binary[6]);
  not not_119 (not_119_out, binary[3]);
  not not_120 (not_120_out, binary[2]);
  not not_121 (not_121_out, binary[5]);
  not not_122 (not_122_out, binary[4]);
  not not_123 (not_123_out, binary[3]);
  not not_124 (not_124_out, binary[5]);
  not not_125 (not_125_out, binary[3]);
  not not_126 (not_126_out, binary[5]);
  not not_127 (not_127_out, binary[3]);
  not not_128 (not_128_out, binary[4]);
  not not_129 (not_129_out, binary[3]);
  not not_130 (not_130_out, binary[4]);
  not not_131 (not_131_out, binary[7]);
  not not_132 (not_132_out, binary[6]);
  not not_133 (not_133_out, binary[5]);
  not not_134 (not_134_out, binary[4]);
  not not_135 (not_135_out, binary[2]);
  not not_136 (not_136_out, binary[1]);
  not not_137 (not_137_out, binary[7]);
  not not_138 (not_138_out, binary[6]);
  not not_139 (not_139_out, binary[5]);
  not not_140 (not_140_out, binary[3]);
  not not_141 (not_141_out, binary[2]);
  not not_142 (not_142_out, binary[7]);
  not not_143 (not_143_out, binary[6]);
  not not_144 (not_144_out, binary[5]);
  not not_145 (not_145_out, binary[1]);
  not not_146 (not_146_out, binary[7]);
  not not_147 (not_147_out, binary[6]);
  not not_148 (not_148_out, binary[4]);
  not not_149 (not_149_out, binary[3]);
  not not_150 (not_150_out, binary[7]);
  not not_151 (not_151_out, binary[6]);
  not not_152 (not_152_out, binary[3]);
  not not_153 (not_153_out, binary[2]);
  not not_154 (not_154_out, binary[1]);
  not not_155 (not_155_out, binary[7]);
  not not_156 (not_156_out, binary[6]);
  not not_157 (not_157_out, binary[2]);
  not not_158 (not_158_out, binary[7]);
  not not_159 (not_159_out, binary[5]);
  not not_160 (not_160_out, binary[4]);
  not not_161 (not_161_out, binary[3]);
  not not_162 (not_162_out, binary[1]);
  not not_163 (not_163_out, binary[7]);
  not not_164 (not_164_out, binary[5]);
  not not_165 (not_165_out, binary[4]);
  not not_166 (not_166_out, binary[7]);
  not not_167 (not_167_out, binary[5]);
  not not_168 (not_168_out, binary[2]);
  not not_169 (not_169_out, binary[1]);
  not not_170 (not_170_out, binary[7]);
  not not_171 (not_171_out, binary[4]);
  not not_172 (not_172_out, binary[3]);
  not not_173 (not_173_out, binary[2]);
  not not_174 (not_174_out, binary[7]);
  not not_175 (not_175_out, binary[4]);
  not not_176 (not_176_out, binary[1]);
  not not_177 (not_177_out, binary[7]);
  not not_178 (not_178_out, binary[3]);
  not not_179 (not_179_out, binary[6]);
  not not_180 (not_180_out, binary[5]);
  not not_181 (not_181_out, binary[4]);
  not not_182 (not_182_out, binary[3]);
  not not_183 (not_183_out, binary[2]);
  not not_184 (not_184_out, binary[1]);
  not not_185 (not_185_out, binary[6]);
  not not_186 (not_186_out, binary[5]);
  not not_187 (not_187_out, binary[4]);
  not not_188 (not_188_out, binary[2]);
  not not_189 (not_189_out, binary[6]);
  not not_190 (not_190_out, binary[5]);
  not not_191 (not_191_out, binary[3]);
  not not_192 (not_192_out, binary[1]);
  not not_193 (not_193_out, binary[6]);
  not not_194 (not_194_out, binary[5]);
  not not_195 (not_195_out, binary[6]);
  not not_196 (not_196_out, binary[4]);
  not not_197 (not_197_out, binary[2]);
  not not_198 (not_198_out, binary[1]);
  not not_199 (not_199_out, binary[6]);
  not not_200 (not_200_out, binary[3]);
  not not_201 (not_201_out, binary[2]);
  not not_202 (not_202_out, binary[6]);
  not not_203 (not_203_out, binary[1]);
  not not_204 (not_204_out, binary[5]);
  not not_205 (not_205_out, binary[4]);
  not not_206 (not_206_out, binary[3]);
  not not_207 (not_207_out, binary[5]);
  not not_208 (not_208_out, binary[3]);
  not not_209 (not_209_out, binary[2]);
  not not_210 (not_210_out, binary[1]);
  not not_211 (not_211_out, binary[5]);
  not not_212 (not_212_out, binary[2]);
  not not_213 (not_213_out, binary[4]);
  not not_214 (not_214_out, binary[3]);
  not not_215 (not_215_out, binary[1]);
  not not_216 (not_216_out, binary[4]);
  not not_217 (not_217_out, binary[2]);
  not not_218 (not_218_out, binary[1]);
  not not_219 (not_219_out, binary[7]);
  not not_220 (not_220_out, binary[6]);
  not not_221 (not_221_out, binary[5]);
  not not_222 (not_222_out, binary[4]);
  not not_223 (not_223_out, binary[3]);
  not not_224 (not_224_out, binary[7]);
  not not_225 (not_225_out, binary[6]);
  not not_226 (not_226_out, binary[5]);
  not not_227 (not_227_out, binary[4]);
  not not_228 (not_228_out, binary[6]);
  not not_229 (not_229_out, binary[5]);
  not not_230 (not_230_out, binary[3]);
  not not_231 (not_231_out, binary[2]);
  not not_232 (not_232_out, binary[1]);
  not not_233 (not_233_out, binary[7]);
  not not_234 (not_234_out, binary[6]);
  not not_235 (not_235_out, binary[5]);
  not not_236 (not_236_out, binary[2]);
  not not_237 (not_237_out, binary[7]);
  not not_238 (not_238_out, binary[6]);
  not not_239 (not_239_out, binary[2]);
  not not_240 (not_240_out, binary[1]);
  not not_241 (not_241_out, binary[7]);
  not not_242 (not_242_out, binary[6]);
  not not_243 (not_243_out, binary[4]);
  not not_244 (not_244_out, binary[3]);
  not not_245 (not_245_out, binary[2]);
  not not_246 (not_246_out, binary[6]);
  not not_247 (not_247_out, binary[4]);
  not not_248 (not_248_out, binary[3]);
  not not_249 (not_249_out, binary[1]);
  not not_250 (not_250_out, binary[7]);
  not not_251 (not_251_out, binary[6]);
  not not_252 (not_252_out, binary[4]);
  not not_253 (not_253_out, binary[7]);
  not not_254 (not_254_out, binary[6]);
  not not_255 (not_255_out, binary[3]);
  not not_256 (not_256_out, binary[7]);
  not not_257 (not_257_out, binary[5]);
  not not_258 (not_258_out, binary[4]);
  not not_259 (not_259_out, binary[3]);
  not not_260 (not_260_out, binary[2]);
  not not_261 (not_261_out, binary[7]);
  not not_262 (not_262_out, binary[5]);
  not not_263 (not_263_out, binary[4]);
  not not_264 (not_264_out, binary[2]);
  not not_265 (not_265_out, binary[5]);
  not not_266 (not_266_out, binary[4]);
  not not_267 (not_267_out, binary[1]);
  not not_268 (not_268_out, binary[7]);
  not not_269 (not_269_out, binary[5]);
  not not_270 (not_270_out, binary[3]);
  not not_271 (not_271_out, binary[7]);
  not not_272 (not_272_out, binary[5]);
  not not_273 (not_273_out, binary[4]);
  not not_274 (not_274_out, binary[3]);
  not not_275 (not_275_out, binary[2]);
  not not_276 (not_276_out, binary[1]);
  not not_277 (not_277_out, binary[7]);
  not not_278 (not_278_out, binary[4]);
  not not_279 (not_279_out, binary[2]);
  not not_280 (not_280_out, binary[7]);
  not not_281 (not_281_out, binary[3]);
  not not_282 (not_282_out, binary[2]);
  not not_283 (not_283_out, binary[3]);
  not not_284 (not_284_out, binary[1]);
  not not_285 (not_285_out, binary[7]);
  not not_286 (not_286_out, binary[6]);
  not not_287 (not_287_out, binary[4]);
  not not_288 (not_288_out, binary[3]);
  not not_289 (not_289_out, binary[6]);
  not not_290 (not_290_out, binary[5]);
  not not_291 (not_291_out, binary[4]);
  not not_292 (not_292_out, binary[2]);
  not not_293 (not_293_out, binary[1]);
  not not_294 (not_294_out, binary[6]);
  not not_295 (not_295_out, binary[5]);
  not not_296 (not_296_out, binary[2]);
  not not_297 (not_297_out, binary[6]);
  not not_298 (not_298_out, binary[5]);
  not not_299 (not_299_out, binary[1]);
  not not_300 (not_300_out, binary[6]);
  not not_301 (not_301_out, binary[4]);
  not not_302 (not_302_out, binary[6]);
  not not_303 (not_303_out, binary[2]);
  not not_304 (not_304_out, binary[1]);
  not not_305 (not_305_out, binary[6]);
  not not_306 (not_306_out, binary[2]);
  not not_307 (not_307_out, binary[4]);
  not not_308 (not_308_out, binary[3]);
  not not_309 (not_309_out, binary[2]);
  not not_310 (not_310_out, binary[5]);
  not not_311 (not_311_out, binary[4]);
  not not_312 (not_312_out, binary[1]);
  not not_313 (not_313_out, binary[5]);
  not not_314 (not_314_out, binary[4]);
  not not_315 (not_315_out, binary[4]);
  not not_316 (not_316_out, binary[1]);
  not not_317 (not_317_out, binary[3]);
  not not_318 (not_318_out, binary[5]);
  not not_319 (not_319_out, binary[2]);
  not not_320 (not_320_out, binary[1]);
  not not_321 (not_321_out, binary[4]);
  not not_322 (not_322_out, binary[2]);
  not not_323 (not_323_out, binary[7]);
  not not_324 (not_324_out, binary[5]);
  not not_325 (not_325_out, binary[4]);
  not not_326 (not_326_out, binary[3]);
  not not_327 (not_327_out, binary[2]);
  not not_328 (not_328_out, binary[7]);
  not not_329 (not_329_out, binary[6]);
  not not_330 (not_330_out, binary[5]);
  not not_331 (not_331_out, binary[3]);
  not not_332 (not_332_out, binary[7]);
  not not_333 (not_333_out, binary[5]);
  not not_334 (not_334_out, binary[4]);
  not not_335 (not_335_out, binary[1]);
  not not_336 (not_336_out, binary[7]);
  not not_337 (not_337_out, binary[6]);
  not not_338 (not_338_out, binary[5]);
  not not_339 (not_339_out, binary[3]);
  not not_340 (not_340_out, binary[2]);
  not not_341 (not_341_out, binary[1]);
  not not_342 (not_342_out, binary[7]);
  not not_343 (not_343_out, binary[6]);
  not not_344 (not_344_out, binary[5]);
  not not_345 (not_345_out, binary[2]);
  not not_346 (not_346_out, binary[7]);
  not not_347 (not_347_out, binary[4]);
  not not_348 (not_348_out, binary[3]);
  not not_349 (not_349_out, binary[2]);
  not not_350 (not_350_out, binary[1]);
  not not_351 (not_351_out, binary[7]);
  not not_352 (not_352_out, binary[6]);
  not not_353 (not_353_out, binary[3]);
  not not_354 (not_354_out, binary[1]);
  not not_355 (not_355_out, binary[7]);
  not not_356 (not_356_out, binary[4]);
  not not_357 (not_357_out, binary[2]);
  not not_358 (not_358_out, binary[7]);
  not not_359 (not_359_out, binary[6]);
  not not_360 (not_360_out, binary[7]);
  not not_361 (not_361_out, binary[6]);
  not not_362 (not_362_out, binary[2]);
  not not_363 (not_363_out, binary[1]);
  not not_364 (not_364_out, binary[7]);
  not not_365 (not_365_out, binary[5]);
  not not_366 (not_366_out, binary[4]);
  not not_367 (not_367_out, binary[1]);
  not not_368 (not_368_out, binary[7]);
  not not_369 (not_369_out, binary[5]);
  not not_370 (not_370_out, binary[1]);
  not not_371 (not_371_out, binary[7]);
  not not_372 (not_372_out, binary[5]);
  not not_373 (not_373_out, binary[3]);
  not not_374 (not_374_out, binary[7]);
  not not_375 (not_375_out, binary[4]);
  not not_376 (not_376_out, binary[3]);
  not not_377 (not_377_out, binary[7]);
  not not_378 (not_378_out, binary[3]);
  not not_379 (not_379_out, binary[1]);
  not not_380 (not_380_out, binary[7]);
  not not_381 (not_381_out, binary[5]);
  not not_382 (not_382_out, binary[4]);
  not not_383 (not_383_out, binary[3]);
  not not_384 (not_384_out, binary[1]);
  not not_385 (not_385_out, binary[6]);
  not not_386 (not_386_out, binary[5]);
  not not_387 (not_387_out, binary[2]);
  not not_388 (not_388_out, binary[1]);
  not not_389 (not_389_out, binary[5]);
  not not_390 (not_390_out, binary[4]);
  not not_391 (not_391_out, binary[6]);
  not not_392 (not_392_out, binary[5]);
  not not_393 (not_393_out, binary[3]);
  not not_394 (not_394_out, binary[2]);
  not not_395 (not_395_out, binary[6]);
  not not_396 (not_396_out, binary[5]);
  not not_397 (not_397_out, binary[1]);
  not not_398 (not_398_out, binary[5]);
  not not_399 (not_399_out, binary[2]);
  not not_400 (not_400_out, binary[1]);
  not not_401 (not_401_out, binary[4]);
  not not_402 (not_402_out, binary[3]);
  not not_403 (not_403_out, binary[2]);
  not not_404 (not_404_out, binary[6]);
  not not_405 (not_405_out, binary[3]);
  not not_406 (not_406_out, binary[4]);
  not not_407 (not_407_out, binary[1]);
  not not_408 (not_408_out, binary[6]);
  not not_409 (not_409_out, binary[3]);
  not not_410 (not_410_out, binary[2]);
  not not_411 (not_411_out, binary[1]);
  not not_412 (not_412_out, binary[6]);
  not not_413 (not_413_out, binary[2]);
  not not_414 (not_414_out, binary[5]);
  not not_415 (not_415_out, binary[4]);
  not not_416 (not_416_out, binary[3]);
  not not_417 (not_417_out, binary[1]);
  not not_418 (not_418_out, binary[5]);
  not not_419 (not_419_out, binary[3]);
  not not_420 (not_420_out, binary[1]);
  not not_421 (not_421_out, binary[5]);
  not not_422 (not_422_out, binary[4]);
  not not_423 (not_423_out, binary[5]);
  not not_424 (not_424_out, binary[4]);
  not not_425 (not_425_out, binary[1]);
  not not_426 (not_426_out, binary[1]);
  not not_427 (not_427_out, binary[3]);
  or or_1 (hundreds[1], and_1_out, and_2_out, and_3_out);
  and and_4 (and_4_out, not_1_out, binary[6], binary[5], binary[2]);
  and and_5 (and_5_out, not_2_out, binary[6], binary[5], binary[3]);
  and and_6 (and_6_out, not_3_out, binary[6], binary[5], binary[4]);
  and and_7 (and_7_out, binary[7], not_4_out);
  and and_8 (and_8_out, binary[7], not_5_out, not_6_out, not_7_out);
  and and_9 (and_9_out, not_8_out, binary[6], not_9_out, binary[4]);
  and and_10 (and_10_out, not_10_out, binary[6], binary[5], not_11_out, not_12_out, not_13_out);
  and and_11 (and_11_out, binary[7], not_14_out, binary[5], binary[4], binary[2]);
  and and_12 (and_12_out, binary[7], not_15_out, binary[5], binary[4], binary[3]);
  and and_13 (and_13_out, binary[7], binary[6], not_16_out, not_17_out, not_18_out);
  and and_14 (and_14_out, not_19_out, binary[5], not_20_out, binary[3]);
  and and_15 (and_15_out, not_21_out, not_22_out, binary[5], binary[4]);
  and and_16 (and_16_out, not_23_out, binary[6], not_24_out, not_25_out);
  and and_17 (and_17_out, binary[7], not_26_out, not_27_out, binary[3], binary[2]);
  and and_18 (and_18_out, binary[7], not_28_out, not_29_out, binary[4]);
  and and_19 (and_19_out, binary[7], not_30_out, binary[5], not_31_out);
  and and_20 (and_20_out, binary[7], not_32_out, binary[5], not_33_out, not_34_out);
  and and_21 (and_21_out, binary[7], binary[6], binary[5], binary[4]);
  and and_22 (and_22_out, not_35_out, not_36_out, not_37_out, binary[4], binary[2]);
  and and_23 (and_23_out, not_38_out, not_39_out, not_40_out, binary[4], binary[3]);
  and and_24 (and_24_out, not_41_out, not_42_out, binary[4], binary[3], binary[2]);
  and and_25 (and_25_out, not_43_out, binary[5], not_44_out, not_45_out);
  and and_26 (and_26_out, not_46_out, binary[6], not_47_out, not_48_out);
  and and_27 (and_27_out, not_49_out, binary[6], binary[5], binary[4], binary[3]);
  and and_28 (and_28_out, binary[7], not_50_out, not_51_out, not_52_out);
  and and_29 (and_29_out, binary[7], not_53_out, not_54_out, not_55_out);
  and and_30 (and_30_out, binary[7], not_56_out, binary[5], not_57_out, not_58_out);
  and and_31 (and_31_out, binary[7], binary[5], not_59_out);
  and and_32 (and_32_out, binary[7], binary[6], not_60_out, binary[4], binary[3], binary[2]);
  and and_33 (and_33_out, not_61_out, not_62_out, not_63_out, binary[3], binary[1]);
  and and_34 (and_34_out, not_64_out, not_65_out, not_66_out, binary[3], binary[2]);
  and and_35 (and_35_out, not_67_out, not_68_out, binary[3], binary[2], binary[1]);
  and and_36 (and_36_out, not_69_out, not_70_out, not_71_out, binary[4], not_72_out, not_73_out);
  and and_37 (and_37_out, not_74_out, not_75_out, binary[5], not_76_out, not_77_out);
  and and_38 (and_38_out, not_78_out, not_79_out, binary[5], not_80_out, binary[1]);
  and and_39 (and_39_out, not_81_out, binary[5], binary[4], not_82_out, binary[2]);
  and and_40 (and_40_out, not_83_out, not_84_out, binary[5], binary[4], binary[3], not_85_out);
  and and_41 (and_41_out, binary[6], not_86_out, not_87_out, not_88_out, binary[2], binary[1]);
  and and_42 (and_42_out, not_89_out, binary[6], not_90_out, not_91_out, binary[3]);
  and and_43 (and_43_out, not_92_out, binary[6], not_93_out, binary[3], binary[1]);
  and and_44 (and_44_out, not_94_out, binary[6], not_95_out, binary[3], binary[2]);
  and and_45 (and_45_out, not_96_out, binary[6], not_97_out, binary[3], binary[2], binary[1]);
  and and_46 (and_46_out, not_98_out, binary[6], binary[5], not_99_out, not_100_out);
  and and_47 (and_47_out, binary[7], not_101_out, not_102_out, not_103_out, binary[1]);
  and and_48 (and_48_out, binary[7], not_104_out, not_105_out, not_106_out, binary[2]);
  and and_49 (and_49_out, binary[7], not_107_out, not_108_out, binary[2], binary[1]);
  and and_50 (and_50_out, binary[7], not_109_out, not_110_out, binary[3], not_111_out);
  and and_51 (and_51_out, binary[7], not_112_out, not_113_out, binary[4], binary[3]);
  and and_52 (and_52_out, binary[7], not_114_out, binary[4], binary[3], not_115_out);
  and and_53 (and_53_out, binary[7], binary[5], not_116_out, binary[3], binary[1]);
  and and_54 (and_54_out, binary[7], binary[5], not_117_out, binary[3], binary[2]);
  and and_55 (and_55_out, binary[7], binary[5], binary[3], binary[2], binary[1]);
  and and_56 (and_56_out, binary[7], not_118_out, binary[5], binary[4], not_119_out, not_120_out);
  and and_57 (and_57_out, binary[7], binary[6], not_121_out, not_122_out, not_123_out);
  and and_58 (and_58_out, binary[7], binary[6], not_124_out, not_125_out, binary[1]);
  and and_59 (and_59_out, binary[7], binary[6], not_126_out, not_127_out, binary[2]);
  and and_60 (and_60_out, binary[7], binary[6], not_128_out, not_129_out, binary[2], binary[1]);
  and and_61 (and_61_out, binary[7], binary[6], binary[5], not_130_out, binary[3]);
  and and_62 (and_62_out, binary[7], binary[6], binary[5], binary[3], binary[1]);
  and and_63 (and_63_out, binary[7], binary[6], binary[5], binary[3], binary[2]);
  and and_64 (and_64_out, not_131_out, not_132_out, not_133_out, not_134_out, binary[3], not_135_out, not_136_out);
  and and_65 (and_65_out, not_137_out, not_138_out, not_139_out, binary[4], not_140_out, not_141_out, binary[1]);
  and and_66 (and_66_out, not_142_out, not_143_out, not_144_out, binary[4], binary[3], binary[2], not_145_out);
  and and_67 (and_67_out, not_146_out, not_147_out, binary[5], not_148_out, not_149_out, binary[2], binary[1]);
  and and_68 (and_68_out, not_150_out, not_151_out, binary[5], binary[4], not_152_out, not_153_out, not_154_out);
  and and_69 (and_69_out, not_155_out, not_156_out, binary[5], binary[4], binary[3], not_157_out, binary[1]);
  and and_70 (and_70_out, not_158_out, binary[6], not_159_out, not_160_out, not_161_out, binary[2], not_162_out);
  and and_71 (and_71_out, not_163_out, binary[6], not_164_out, not_165_out, binary[3], binary[2], binary[1]);
  and and_72 (and_72_out, not_166_out, binary[6], not_167_out, binary[4], binary[3], not_168_out, not_169_out);
  and and_73 (and_73_out, not_170_out, binary[6], binary[5], not_171_out, not_172_out, not_173_out, binary[1]);
  and and_74 (and_74_out, not_174_out, binary[6], binary[5], not_175_out, binary[3], binary[2], not_176_out);
  and and_75 (and_75_out, not_177_out, binary[6], binary[5], binary[4], not_178_out, binary[2], binary[1]);
  and and_76 (and_76_out, binary[7], not_179_out, not_180_out, not_181_out, not_182_out, not_183_out, not_184_out);
  and and_77 (and_77_out, binary[7], not_185_out, not_186_out, not_187_out, binary[3], not_188_out, binary[1]);
  and and_78 (and_78_out, binary[7], not_189_out, not_190_out, binary[4], not_191_out, binary[2], not_192_out);
  and and_79 (and_79_out, binary[7], not_193_out, not_194_out, binary[4], binary[3], binary[2], binary[1]);
  and and_80 (and_80_out, binary[7], not_195_out, binary[5], not_196_out, binary[3], not_197_out, not_198_out);
  and and_81 (and_81_out, binary[7], not_199_out, binary[5], binary[4], not_200_out, not_201_out, binary[1]);
  and and_82 (and_82_out, binary[7], not_202_out, binary[5], binary[4], binary[3], binary[2], not_203_out);
  and and_83 (and_83_out, binary[7], binary[6], not_204_out, not_205_out, not_206_out, binary[2], binary[1]);
  and and_84 (and_84_out, binary[7], binary[6], not_207_out, binary[4], not_208_out, not_209_out, not_210_out);
  and and_85 (and_85_out, binary[7], binary[6], not_211_out, binary[4], binary[3], not_212_out, binary[1]);
  and and_86 (and_86_out, binary[7], binary[6], binary[5], not_213_out, not_214_out, binary[2], not_215_out);
  and and_87 (and_87_out, binary[7], binary[6], binary[5], not_216_out, binary[3], binary[2], binary[1]);
  and and_88 (and_88_out, binary[7], binary[6], binary[5], binary[4], binary[3], not_217_out, not_218_out);
  and and_89 (and_89_out, not_219_out, not_220_out, not_221_out, not_222_out, not_223_out, binary[2]);
  and and_90 (and_90_out, not_224_out, not_225_out, not_226_out, not_227_out, binary[2], binary[1]);
  and and_91 (and_91_out, not_228_out, not_229_out, binary[4], not_230_out, not_231_out, not_232_out);
  and and_92 (and_92_out, not_233_out, not_234_out, not_235_out, binary[4], binary[3], not_236_out);
  and and_93 (and_93_out, not_237_out, not_238_out, binary[4], binary[3], not_239_out, not_240_out);
  and and_94 (and_94_out, not_241_out, not_242_out, binary[5], not_243_out, not_244_out, not_245_out, binary[1]);
  and and_95 (and_95_out, not_246_out, binary[5], not_247_out, not_248_out, binary[2], not_249_out);
  and and_96 (and_96_out, not_250_out, not_251_out, binary[5], not_252_out, binary[3], binary[2]);
  and and_97 (and_97_out, not_253_out, not_254_out, binary[5], binary[4], not_255_out, binary[2], binary[1]);
  and and_98 (and_98_out, not_256_out, binary[6], not_257_out, not_258_out, not_259_out, not_260_out);
  and and_99 (and_99_out, not_261_out, binary[6], not_262_out, not_263_out, not_264_out, binary[1]);
  and and_100 (and_100_out, binary[6], not_265_out, not_266_out, binary[3], binary[2], not_267_out);
  and and_101 (and_101_out, not_268_out, binary[6], not_269_out, binary[4], not_270_out, binary[2]);
  and and_102 (and_102_out, not_271_out, binary[6], not_272_out, binary[4], binary[2], binary[1]);
  and and_103 (and_103_out, binary[6], binary[5], not_273_out, not_274_out, not_275_out, not_276_out);
  and and_104 (and_104_out, not_277_out, binary[6], binary[5], not_278_out, binary[3], not_279_out);
  and and_105 (and_105_out, not_280_out, binary[6], binary[5], binary[4], not_281_out, not_282_out, binary[1]);
  and and_106 (and_106_out, binary[6], binary[5], binary[4], not_283_out, binary[2], not_284_out);
  and and_107 (and_107_out, not_285_out, binary[6], binary[5], binary[4], binary[3], binary[2]);
  and and_108 (and_108_out, binary[7], not_286_out, not_287_out, not_288_out, binary[2], binary[1]);
  and and_109 (and_109_out, binary[7], not_289_out, not_290_out, not_291_out, binary[3], not_292_out, not_293_out);
  and and_110 (and_110_out, binary[7], not_294_out, not_295_out, binary[4], not_296_out, binary[1]);
  and and_111 (and_111_out, binary[7], not_297_out, not_298_out, binary[4], binary[3], binary[2], not_299_out);
  and and_112 (and_112_out, binary[7], not_300_out, binary[5], not_301_out, binary[2], binary[1]);
  and and_113 (and_113_out, binary[7], not_302_out, binary[5], binary[4], not_303_out, not_304_out);
  and and_114 (and_114_out, binary[7], not_305_out, binary[5], binary[4], binary[3], not_306_out);
  and and_115 (and_115_out, binary[7], binary[6], not_307_out, not_308_out, not_309_out, binary[1]);
  and and_116 (and_116_out, binary[7], binary[6], not_310_out, not_311_out, binary[2], not_312_out);
  and and_117 (and_117_out, binary[7], binary[6], not_313_out, not_314_out, binary[3], binary[2]);
  and and_118 (and_118_out, binary[7], binary[6], not_315_out, binary[3], binary[2], not_316_out);
  and and_119 (and_119_out, binary[7], binary[6], binary[4], not_317_out, binary[2], binary[1]);
  and and_120 (and_120_out, binary[7], binary[6], not_318_out, binary[4], binary[3], not_319_out, not_320_out);
  and and_121 (and_121_out, binary[7], binary[6], binary[5], not_321_out, not_322_out, binary[1]);
  and and_122 (and_122_out, binary[7], binary[6], binary[5], binary[4], binary[2], binary[1]);
  and and_123 (and_123_out, not_323_out, not_324_out, not_325_out, not_326_out, not_327_out, binary[1]);
  and and_124 (and_124_out, not_328_out, not_329_out, not_330_out, not_331_out, binary[2], binary[1]);
  and and_125 (and_125_out, not_332_out, not_333_out, not_334_out, binary[3], binary[2], not_335_out);
  and and_126 (and_126_out, not_336_out, not_337_out, not_338_out, binary[4], not_339_out, not_340_out, not_341_out);
  and and_127 (and_127_out, not_342_out, not_343_out, not_344_out, binary[4], binary[3], not_345_out, binary[1]);
  and and_128 (and_128_out, not_346_out, binary[5], not_347_out, not_348_out, not_349_out, not_350_out);
  and and_129 (and_129_out, not_351_out, not_352_out, binary[5], not_353_out, binary[2], not_354_out);
  and and_130 (and_130_out, not_355_out, binary[5], not_356_out, binary[3], not_357_out, binary[1]);
  and and_131 (and_131_out, not_358_out, not_359_out, binary[5], binary[3], binary[2], binary[1]);
  and and_132 (and_132_out, not_360_out, not_361_out, binary[5], binary[4], binary[3], not_362_out, not_363_out);
  and and_133 (and_133_out, not_364_out, binary[6], not_365_out, not_366_out, binary[3], not_367_out);
  and and_134 (and_134_out, not_368_out, binary[6], not_369_out, binary[3], binary[2], not_370_out);
  and and_135 (and_135_out, not_371_out, binary[6], not_372_out, binary[4], not_373_out, binary[1]);
  and and_136 (and_136_out, not_374_out, binary[6], binary[5], not_375_out, not_376_out, binary[2], binary[1]);
  and and_137 (and_137_out, not_377_out, binary[6], binary[5], binary[4], not_378_out, not_379_out);
  and and_138 (and_138_out, not_380_out, binary[6], binary[5], binary[4], binary[3], binary[1]);
  and and_139 (and_139_out, binary[7], not_381_out, not_382_out, not_383_out, binary[2], not_384_out);
  and and_140 (and_140_out, binary[7], not_385_out, not_386_out, binary[3], not_387_out, not_388_out);
  and and_141 (and_141_out, binary[7], not_389_out, not_390_out, binary[3], binary[2], binary[1]);
  and and_142 (and_142_out, binary[7], not_391_out, not_392_out, binary[4], not_393_out, not_394_out, binary[1]);
  and and_143 (and_143_out, binary[7], not_395_out, not_396_out, binary[4], binary[3], not_397_out);
  and and_144 (and_144_out, binary[7], not_398_out, binary[4], binary[3], not_399_out, not_400_out);
  and and_145 (and_145_out, binary[7], binary[5], not_401_out, not_402_out, not_403_out, binary[1]);
  and and_146 (and_146_out, binary[7], not_404_out, binary[5], not_405_out, binary[2], binary[1]);
  and and_147 (and_147_out, binary[7], binary[5], not_406_out, binary[3], binary[2], not_407_out);
  and and_148 (and_148_out, binary[7], not_408_out, binary[5], binary[4], not_409_out, not_410_out, not_411_out);
  and and_149 (and_149_out, binary[7], not_412_out, binary[5], binary[4], binary[3], not_413_out, binary[1]);
  and and_150 (and_150_out, binary[7], binary[6], not_414_out, not_415_out, not_416_out, not_417_out);
  and and_151 (and_151_out, binary[7], binary[6], not_418_out, not_419_out, binary[2], not_420_out);
  and and_152 (and_152_out, binary[7], binary[6], not_421_out, not_422_out, binary[3], binary[1]);
  and and_153 (and_153_out, binary[7], binary[6], not_423_out, binary[3], binary[2], binary[1]);
  and and_154 (and_154_out, binary[7], binary[6], binary[5], not_424_out, binary[3], not_425_out);
  and and_155 (and_155_out, binary[7], binary[6], binary[5], binary[3], binary[2], not_426_out);
  and and_156 (and_156_out, binary[7], binary[6], binary[5], binary[4], not_427_out, binary[1]);
  or or_2 (hundreds[0], and_4_out, and_5_out, and_6_out, and_7_out, and_8_out);
  or or_3 (tens[3], and_9_out, and_10_out, and_11_out, and_12_out, and_13_out);
  or or_4 (tens[2], and_14_out, and_15_out, and_16_out, and_17_out, and_18_out, and_19_out, and_20_out, and_21_out);
  or or_5 (tens[1], and_22_out, and_23_out, and_24_out, and_25_out, and_26_out, and_27_out, and_28_out, and_29_out, and_30_out, and_31_out, and_32_out);
  or or_6 (or_6_out, and_89_out, and_90_out, and_91_out, and_92_out, and_93_out, and_94_out, and_95_out, and_96_out, and_97_out, and_98_out, and_99_out, and_100_out, and_101_out, and_102_out, and_103_out, and_104_out, and_105_out);
  or or_7 (or_7_out, and_106_out, and_107_out, and_108_out, and_109_out, and_110_out, and_111_out, and_112_out, and_113_out, and_114_out, and_115_out, and_116_out, and_117_out, and_118_out, and_119_out, and_120_out, and_121_out, and_122_out);
  or or_8 (or_8_out, and_123_out, and_124_out, and_125_out, and_126_out, and_127_out, and_128_out, and_129_out, and_130_out, and_131_out, and_132_out, and_133_out, and_134_out, and_135_out, and_136_out, and_137_out, and_138_out, and_139_out);
  or or_9 (or_9_out, and_140_out, and_141_out, and_142_out, and_143_out, and_144_out, and_145_out, and_146_out, and_147_out, and_148_out, and_149_out, and_150_out, and_151_out, and_152_out, and_153_out, and_154_out, and_155_out, and_156_out);
  or or_10 (tens[0], and_33_out, and_34_out, and_35_out, and_36_out, and_37_out, and_38_out, and_39_out, and_40_out, and_41_out, and_42_out, and_43_out, and_44_out, and_45_out, and_46_out, and_47_out, and_48_out, and_49_out, and_50_out, and_51_out, and_52_out, and_53_out, and_54_out, and_55_out, and_56_out, and_57_out, and_58_out, and_59_out, and_60_out, and_61_out, and_62_out, and_63_out);
  or or_11 (units[3], and_64_out, and_65_out, and_66_out, and_67_out, and_68_out, and_69_out, and_70_out, and_71_out, and_72_out, and_73_out, and_74_out, and_75_out, and_76_out, and_77_out, and_78_out, and_79_out, and_80_out, and_81_out, and_82_out, and_83_out, and_84_out, and_85_out, and_86_out, and_87_out, and_88_out);
  or or_12 (units[2], or_6_out, or_7_out);
  or or_13 (units[1], or_8_out, or_9_out);

  assign hundreds[3:2] = 2'b00;
  assign units[0] = binary[0];

  // Other names for the same wires on the sheet: _0 = binary[0]; u0 = binary[0]; _1 = binary[1]; _2 = binary[2];
  //   _3 = binary[3]; _4 = binary[4]; _5 = binary[5]; _6 = binary[6]; _7 = binary[7]; h0 = hundreds[0];
  //   h1 = hundreds[1]; t0 = tens[0]; t1 = tens[1]; t2 = tens[2]; t3 = tens[3]; u1 = units[1]; u2 = units[2];
  //   u3 = units[3]
endmodule

module BIN_TO_BCD_R (
  input  [7:0] binary,
  output [3:0] units,
  output [3:0] tens,
  output [3:0] hundreds
);

  ROM #(.dataWidth(12)) rom_1 (.addr(binary), .data({hundreds, tens, units}), .sel(1'b1));

  // Notes on the sheet:
  //   contents of rom_1 (hex, n*v repeats v):
  //   0 1 2 3 4 5 6 7 8 9 10 11 12 13 14 15 16 17 18 19 20 21 22 23 24 25 26 27 28 29 30 31 32 33 34 35 36
  //   37 38 39 40 41 42 43 44 45 46 47 48 49 50 51 52 53 54 55 56 57 58 59 60 61 62 63 64 65 66 67 68 69
  //   70 71 72 73 74 75 76 77 78 79 80 81 82 83 84 85 86 87 88 89 90 91 92 93 94 95 96 97 98 99 100 101
  //   102 103 104 105 106 107 108 109 110 111 112 113 114 115 116 117 118 119 120 121 122 123 124 125 126
  //   127 128 129 130 131 132 133 134 135 136 137 138 139 140 141 142 143 144 145 146 147 148 149 150 151
  //   152 153 154 155 156 157 158 159 160 161 162 163 164 165 166 167 168 169 170 171 172 173 174 175 176
  //   177 178 179 180 181 182 183 184 185 186 187 188 189 190 191 192 193 194 195 196 197 198 199 200 201
  //   202 203 204 205 206 207 208 209 210 211 212 213 214 215 216 217 218 219 220 221 222 223 224 225 226
  //   227 228 229 230 231 232 233 234 235 236 237 238 239 240 241 242 243 244 245 246 247 248 249 250 251
  //   252 253 254 255
endmodule

module TWOSCOMP_TO_BCD (
  input  [7:0] binary,
  output [3:0] units,
  output [3:0] tens,
  output [3:0] hundreds,
  output sign
);

  wire or_1_out;

  or or_1 (or_1_out, binary[0], binary[1], binary[2], binary[3], binary[4], binary[5], binary[6]);
  and and_1 (sign, or_1_out, binary[7]);
  ROM #(.dataWidth(12)) rom_1 (.addr(binary), .data({hundreds, tens, units}), .sel(1'b1));

  // Notes on the sheet:
  //   contents of rom_1 (hex, n*v repeats v):
  //   0 1 2 3 4 5 6 7 8 9 10 11 12 13 14 15 16 17 18 19 20 21 22 23 24 25 26 27 28 29 30 31 32 33 34 35 36
  //   37 38 39 40 41 42 43 44 45 46 47 48 49 50 51 52 53 54 55 56 57 58 59 60 61 62 63 64 65 66 67 68 69
  //   70 71 72 73 74 75 76 77 78 79 80 81 82 83 84 85 86 87 88 89 90 91 92 93 94 95 96 97 98 99 100 101
  //   102 103 104 105 106 107 108 109 110 111 112 113 114 115 116 117 118 119 120 121 122 123 124 125 126
  //   127 0 127 126 125 124 123 122 121 120 119 118 117 116 115 114 113 112 111 110 109 108 107 106 105
  //   104 103 102 101 100 99 98 97 96 95 94 93 92 91 90 89 88 87 86 85 84 83 82 81 80 79 78 77 76 75 74 73
  //   72 71 70 69 68 67 66 65 64 63 62 61 60 59 58 57 56 55 54 53 52 51 50 49 48 47 46 45 44 43 42 41 40
  //   39 38 37 36 35 34 33 32 31 30 29 28 27 26 25 24 23 22 21 20 19 18 17 16 15 14 13 12 11 10 9 8 7 6 5
  //   4 3 2 1
endmodule
